// Logisim project ADDER.circ as structural Verilog: 1 circuit, main circuit main
module main (
  input  [31:0] A,
  input  [31:0] B,
  input  CLK,
  input  ENABLE,
  output [31:0] SUM
);

  wire main_1_c_out, main_2_c_out, main_3_c_out, main_4_c_out, main_5_c_out, main_6_c_out, main_7_c_out,
       main_8_c_out, main_9_c_out, main_10_c_out, main_11_c_out, main_12_c_out, main_13_c_out, main_14_c_out,
       main_15_c_out, main_16_c_out, main_17_c_out, main_18_c_out, main_19_c_out, main_20_c_out,
       main_21_c_out, main_22_c_out, main_23_c_out, main_24_c_out, main_25_c_out, main_26_c_out,
       main_27_c_out, main_28_c_out, main_29_c_out, main_30_c_out, main_31_c_out, not_1_out;
  wire [31:0] main_1_sum;

  not not_1 (not_1_out, 1'b1);
  FULL_ADDER_1_BIT_main main_1 (.A(A[0]), .B(B[0]), .C_IN(not_1_out), .SUM(main_1_sum[0]), .C_OUT(main_1_c_out));
  FULL_ADDER_1_BIT_main main_2 (.A(A[1]), .B(B[1]), .C_IN(main_1_c_out), .SUM(main_1_sum[1]), .C_OUT(main_2_c_out));
  FULL_ADDER_1_BIT_main main_3 (.A(A[2]), .B(B[2]), .C_IN(main_2_c_out), .SUM(main_1_sum[2]), .C_OUT(main_3_c_out));
  FULL_ADDER_1_BIT_main main_4 (.A(A[3]), .B(B[3]), .C_IN(main_3_c_out), .SUM(main_1_sum[3]), .C_OUT(main_4_c_out));
  FULL_ADDER_1_BIT_main main_5 (.A(A[4]), .B(B[4]), .C_IN(main_4_c_out), .SUM(main_1_sum[4]), .C_OUT(main_5_c_out));
  FULL_ADDER_1_BIT_main main_6 (.A(A[5]), .B(B[5]), .C_IN(main_5_c_out), .SUM(main_1_sum[5]), .C_OUT(main_6_c_out));
  FULL_ADDER_1_BIT_main main_7 (.A(A[6]), .B(B[6]), .C_IN(main_6_c_out), .SUM(main_1_sum[6]), .C_OUT(main_7_c_out));
  FULL_ADDER_1_BIT_main main_8 (.A(A[7]), .B(B[7]), .C_IN(main_7_c_out), .SUM(main_1_sum[7]), .C_OUT(main_8_c_out));
  FULL_ADDER_1_BIT_main main_9 (.A(A[8]), .B(B[8]), .C_IN(main_8_c_out), .SUM(main_1_sum[8]), .C_OUT(main_9_c_out));
  FULL_ADDER_1_BIT_main main_10 (.A(A[9]), .B(B[9]), .C_IN(main_9_c_out), .SUM(main_1_sum[9]), .C_OUT(main_10_c_out));
  FULL_ADDER_1_BIT_main main_11 (
    .A(A[10]), .B(B[10]), .C_IN(main_10_c_out), .SUM(main_1_sum[10]), .C_OUT(main_11_c_out));
  FULL_ADDER_1_BIT_main main_12 (
    .A(A[11]), .B(B[11]), .C_IN(main_11_c_out), .SUM(main_1_sum[11]), .C_OUT(main_12_c_out));
  FULL_ADDER_1_BIT_main main_13 (
    .A(A[12]), .B(B[12]), .C_IN(main_12_c_out), .SUM(main_1_sum[12]), .C_OUT(main_13_c_out));
  FULL_ADDER_1_BIT_main main_14 (
    .A(A[13]), .B(B[13]), .C_IN(main_13_c_out), .SUM(main_1_sum[13]), .C_OUT(main_14_c_out));
  FULL_ADDER_1_BIT_main main_15 (
    .A(A[14]), .B(B[14]), .C_IN(main_14_c_out), .SUM(main_1_sum[14]), .C_OUT(main_15_c_out));
  FULL_ADDER_1_BIT_main main_16 (
    .A(A[15]), .B(B[15]), .C_IN(main_15_c_out), .SUM(main_1_sum[15]), .C_OUT(main_16_c_out));
  FULL_ADDER_1_BIT_main main_17 (
    .A(A[16]), .B(B[16]), .C_IN(main_16_c_out), .SUM(main_1_sum[16]), .C_OUT(main_17_c_out));
  FULL_ADDER_1_BIT_main main_18 (
    .A(A[17]), .B(B[17]), .C_IN(main_17_c_out), .SUM(main_1_sum[17]), .C_OUT(main_18_c_out));
  FULL_ADDER_1_BIT_main main_19 (
    .A(A[18]), .B(B[18]), .C_IN(main_18_c_out), .SUM(main_1_sum[18]), .C_OUT(main_19_c_out));
  FULL_ADDER_1_BIT_main main_20 (
    .A(A[19]), .B(B[19]), .C_IN(main_19_c_out), .SUM(main_1_sum[19]), .C_OUT(main_20_c_out));
  FULL_ADDER_1_BIT_main main_21 (
    .A(A[20]), .B(B[20]), .C_IN(main_20_c_out), .SUM(main_1_sum[20]), .C_OUT(main_21_c_out));
  FULL_ADDER_1_BIT_main main_22 (
    .A(A[21]), .B(B[21]), .C_IN(main_21_c_out), .SUM(main_1_sum[21]), .C_OUT(main_22_c_out));
  FULL_ADDER_1_BIT_main main_23 (
    .A(A[22]), .B(B[22]), .C_IN(main_22_c_out), .SUM(main_1_sum[22]), .C_OUT(main_23_c_out));
  FULL_ADDER_1_BIT_main main_24 (
    .A(A[23]), .B(B[23]), .C_IN(main_23_c_out), .SUM(main_1_sum[23]), .C_OUT(main_24_c_out));
  FULL_ADDER_1_BIT_main main_25 (
    .A(A[24]), .B(B[24]), .C_IN(main_24_c_out), .SUM(main_1_sum[24]), .C_OUT(main_25_c_out));
  FULL_ADDER_1_BIT_main main_26 (
    .A(A[25]), .B(B[25]), .C_IN(main_25_c_out), .SUM(main_1_sum[25]), .C_OUT(main_26_c_out));
  FULL_ADDER_1_BIT_main main_27 (
    .A(A[26]), .B(B[26]), .C_IN(main_26_c_out), .SUM(main_1_sum[26]), .C_OUT(main_27_c_out));
  FULL_ADDER_1_BIT_main main_28 (
    .A(A[27]), .B(B[27]), .C_IN(main_27_c_out), .SUM(main_1_sum[27]), .C_OUT(main_28_c_out));
  FULL_ADDER_1_BIT_main main_29 (
    .A(A[28]), .B(B[28]), .C_IN(main_28_c_out), .SUM(main_1_sum[28]), .C_OUT(main_29_c_out));
  FULL_ADDER_1_BIT_main main_30 (
    .A(A[29]), .B(B[29]), .C_IN(main_29_c_out), .SUM(main_1_sum[29]), .C_OUT(main_30_c_out));
  FULL_ADDER_1_BIT_main main_31 (
    .A(A[30]), .B(B[30]), .C_IN(main_30_c_out), .SUM(main_1_sum[30]), .C_OUT(main_31_c_out));
  FULL_ADDER_1_BIT_main main_32 (.A(A[31]), .B(B[31]), .C_IN(main_31_c_out), .SUM(main_1_sum[31]));  // open: C_OUT
  Register #(.width(32)) register_1 (.D(main_1_sum), .en(ENABLE), .Q(SUM), .clk(CLK));  // open: clr
endmodule
