// Logisim project FULL_ADDER_1-BIT.circ as structural Verilog: 1 circuit, main circuit main
module main (
  input  A,
  input  B,
  input  C_IN,
  output SUM,
  output C_OUT
);

  wire and_1_out, and_2_out, xor_1_out;

  xor xor_1 (xor_1_out, A, B);
  and and_1 (and_1_out, C_IN, xor_1_out);
  and and_2 (and_2_out, B, A);
  xor xor_2 (SUM, xor_1_out, C_IN);
  or or_1 (C_OUT, and_1_out, and_2_out);
endmodule
