// Logisim project SHIFTER.circ as structural Verilog: 1 circuit, main circuit main
module main (
  input  [31:0] SHFT_RM,
  input  [31:0] SHFT_LM,
  input  ENABLE,
  input  CLK,
  output [31:0] RESULT_R,
  output [31:0] RESULT_L
);

  wire [31:31] not_1_out;

  not not_1 (not_1_out[31], 1'b1);
  Register #(.width(32)) register_1 (
    .D({SHFT_LM[0], SHFT_RM[31:1]}), .en(ENABLE), .Q(RESULT_R), .clk(CLK));  // open: clr
  Register #(.width(32)) register_2 (
    .D({not_1_out[31], SHFT_LM[31:1]}), .en(ENABLE), .Q(RESULT_L), .clk(CLK));  // open: clr
endmodule
