// Logisim project control.circ as structural Verilog: 1 circuit, main circuit main
module main (
  input  S,
  input  CT,
  input  PR,
  input  CLK,
  output A,
  output SH,
  output C
);

  wire and_1_out, and_2_out, and_3_out, and_4_out, and_5_out, and_6_out, and_7_out, and_8_out, and_9_out,
       and_10_out, and_11_out, and_12_out, and_13_out, and_14_out;
  wire [1:0] or_2_out, register_1_q;

  and and_1 (and_1_out, register_1_q[1], register_1_q[0]);
  and and_2 (and_2_out, ~register_1_q[0], ~register_1_q[1], ~PR, S);  // AND_Gate
  and and_3 (and_3_out, ~register_1_q[1], register_1_q[0]);  // AND_Gate
  and and_4 (and_4_out, register_1_q[1], ~register_1_q[0], ~PR, ~CT);  // AND_Gate
  and and_5 (and_5_out, register_1_q[1], ~register_1_q[0], CT);  // AND_Gate
  and and_6 (and_6_out, register_1_q[1], register_1_q[0]);
  and and_7 (and_7_out, ~register_1_q[0], ~register_1_q[1], S, PR);  // AND_Gate
  and and_8 (and_8_out, register_1_q[1], ~register_1_q[0], PR, ~CT);  // AND_Gate
  and and_9 (and_9_out, register_1_q[1], ~register_1_q[0], CT);  // AND_Gate
  and and_10 (and_10_out, ~register_1_q[1], ~register_1_q[0], S, PR);  // AND_Gate
  and and_11 (and_11_out, register_1_q[1], ~register_1_q[0], PR, ~CT);  // AND_Gate
  and and_12 (and_12_out, ~register_1_q[1], ~register_1_q[0], S, ~PR);  // AND_Gate
  and and_13 (and_13_out, ~register_1_q[1], register_1_q[0]);  // AND_Gate
  and and_14 (and_14_out, register_1_q[1], ~register_1_q[0], ~PR, ~CT);  // AND_Gate
  or or_1 (or_2_out[1], and_2_out, and_3_out, and_1_out, and_4_out, and_5_out);
  or or_2 (or_2_out[0], and_7_out, and_8_out, and_6_out, and_9_out);
  or or_3 (A, and_10_out, and_11_out);
  or or_4 (C, and_12_out, and_13_out, and_14_out);
  Register #(.width(2)) register_1 (.D(or_2_out), .Q(register_1_q), .clk(CLK));  // open: en, clr

  assign SH = C;
endmodule
