// Logisim project datapath.circ as structural Verilog: 1 circuit, main circuit main
module main (
  input  [31:0] Multiplier,
  input  [31:0] Multiplicand,
  input  CLK,
  input  A,
  input  SH,
  input  C,
  output CT,
  output PR,
  output [31:0] RESULT_R,
  output [31:0] RESULT_L
);

  wire comparator_1_eq, or_1_out, register_1_q;
  wire [4:0] not_7_out;
  wire [5:0] counter_1_q, not_4_out;
  wire [31:0] main_1_sum, multiplexer_1_out, multiplexer_2_out, register_2_q;

  ADDER_main main_1 (.A(Multiplicand), .B(RESULT_L), .CLK(CLK), .ENABLE(A), .SUM(main_1_sum));
  Register #(.width(1)) register_1 (.D(A), .en(or_1_out), .Q(register_1_q), .clk(CLK));  // open: clr
  or or_1 (or_1_out, A, SH);
  Register #(.width(32)) register_2 (.D(Multiplier), .en(comparator_1_eq), .Q(register_2_q), .clk(CLK));  // open: clr
  not not_1 (not_4_out[3], 1'b1);
  not not_2 (not_4_out[4], 1'b1);
  not not_3 (not_4_out[5], 1'b1);
  Multiplexer #(.width(32)) multiplexer_1 (
    .in0(RESULT_R), .in1(register_2_q), .out(multiplexer_1_out), .sel(comparator_1_eq));  // open: en
  Multiplexer #(.width(32)) multiplexer_2 (
    .in0(RESULT_L), .in1(main_1_sum), .out(multiplexer_2_out), .sel(register_1_q));  // open: en
  not not_4 (not_4_out[0], 1'b1);
  not not_5 (not_4_out[1], 1'b1);
  not not_6 (not_4_out[2], 1'b1);
  not not_7 (not_7_out[0], 1'b1);
  not not_8 (not_7_out[1], 1'b1);
  not not_9 (not_7_out[2], 1'b1);
  not not_10 (not_7_out[3], 1'b1);
  not not_11 (not_7_out[4], 1'b1);
  Counter #(.width(6), .max('h3f)) counter_1 (
    .D(counter_1_q), .count(C), .Q(counter_1_q), .clk(CLK));  // open: load, carry, clr
  SHIFTER_main main_2 (
    .SHFT_RM(multiplexer_1_out), .SHFT_LM(multiplexer_2_out), .ENABLE(SH), .CLK(CLK), .RESULT_R(RESULT_R),
    .RESULT_L(RESULT_L));
  Comparator #(.width(6), .mode("unsigned")) comparator_1 (
    .a(not_4_out), .b(counter_1_q), .eq(comparator_1_eq));  // open: gt, lt
  Comparator #(.width(6), .mode("unsigned")) comparator_2 (
    .a({1'b1, not_7_out}), .b(counter_1_q), .eq(CT));  // open: gt, lt
  Comparator #(.width(1)) comparator_3 (.a(multiplexer_1_out[0]), .b(1'b1), .eq(PR));  // open: gt, lt
endmodule
