// Logisim project mult32.circ as structural Verilog: 1 circuit, main circuit main
module main (
  input  START,
  input  [31:0] MULTIPLICAND,
  input  [31:0] MULTIPLIER,
  output [31:0] RESULT_R,
  output [31:0] RESULT_L
);

  wire clock_1_out, main_1_a, main_1_c, main_1_sh, main_2_ct, main_2_pr;

  Clock clock_1 (.out(clock_1_out));
  control_main main_1 (
    .S(START), .CT(main_2_ct), .PR(main_2_pr), .CLK(clock_1_out), .A(main_1_a), .SH(main_1_sh), .C(main_1_c));
  datapath_main main_2 (
    .Multiplier(MULTIPLIER), .Multiplicand(MULTIPLICAND), .CLK(clock_1_out), .A(main_1_a), .SH(main_1_sh),
    .C(main_1_c), .CT(main_2_ct), .PR(main_2_pr), .RESULT_R(RESULT_R), .RESULT_L(RESULT_L));
endmodule
