// Logisim project 7-segment.circ as structural Verilog: 1 circuit, main circuit HEX
module HEX (
  input  CLK,
  input  X,
  output X6,
  output X5,
  output X4,
  output X3,
  output X2,
  output X1,
  output X0
);

  wire and_1_out, and_2_out, and_3_out, and_4_out, and_5_out, and_6_out, and_7_out, and_8_out, and_9_out,
       and_10_out, and_11_out, and_12_out, and_13_out, and_14_out, and_15_out, and_16_out, and_17_out,
       and_18_out, and_19_out, and_20_out, and_21_out, and_22_out, and_23_out, and_24_out, and_25_out,
       and_26_out, and_27_out, and_28_out, and_29_out, and_30_out, and_31_out, and_32_out, and_33_out,
       and_34_out, and_35_out, and_36_out, and_37_out, and_38_out, and_39_out, and_40_out, and_41_out,
       and_42_out, and_43_out, and_44_out, and_45_out, and_46_out, and_47_out, and_48_out, and_49_out,
       and_50_out, and_51_out, and_52_out, and_53_out, and_54_out, and_55_out, and_56_out, and_57_out,
       and_58_out, and_59_out, and_60_out, and_61_out, and_62_out, and_63_out, and_64_out, and_65_out,
       not_1_out, not_2_out, not_3_out, not_4_out, not_5_out, not_6_out, not_7_out, not_8_out, not_9_out,
       not_10_out, not_11_out, not_12_out, not_13_out, not_14_out, not_15_out, not_16_out, not_17_out,
       not_18_out, not_19_out, not_20_out, not_21_out, not_22_out, not_23_out, not_24_out, not_25_out,
       not_26_out, not_27_out, not_28_out, not_29_out, not_30_out, not_31_out, not_32_out, not_33_out,
       not_34_out, not_35_out, not_36_out, not_37_out, not_38_out, not_39_out, not_40_out, not_41_out,
       not_42_out, not_43_out, not_44_out, not_45_out, not_46_out, not_47_out, not_48_out, not_49_out,
       not_50_out, not_51_out, not_52_out, not_53_out, not_54_out, not_55_out, not_56_out, not_57_out,
       not_58_out, not_59_out, not_60_out, not_61_out, not_62_out, not_63_out, not_64_out, not_65_out,
       not_66_out, not_67_out, not_68_out, not_69_out, not_70_out, not_71_out, not_72_out, not_73_out,
       not_74_out, not_75_out, not_76_out, not_77_out, not_78_out, not_79_out, not_80_out, not_81_out,
       not_82_out, not_83_out, not_84_out, not_85_out, not_86_out, not_87_out, not_88_out, not_89_out,
       not_90_out, not_91_out, not_92_out;
  wire [4:0] register_1_q;
  wire [4:1] or_4_out;

  Register #(.width(5)) register_1 (.D({or_4_out, X}), .en(1'b1), .Q(register_1_q), .clk(CLK));  // open: clr
  not not_1 (not_1_out, X);
  not not_2 (not_2_out, register_1_q[1]);
  not not_3 (not_3_out, register_1_q[0]);
  not not_4 (not_4_out, register_1_q[3]);
  not not_5 (not_5_out, X);
  not not_6 (not_6_out, register_1_q[2]);
  not not_7 (not_7_out, register_1_q[1]);
  not not_8 (not_8_out, register_1_q[0]);
  not not_9 (not_9_out, register_1_q[4]);
  not not_10 (not_10_out, register_1_q[2]);
  not not_11 (not_11_out, X);
  not not_12 (not_12_out, register_1_q[1]);
  not not_13 (not_13_out, register_1_q[0]);
  not not_14 (not_14_out, register_1_q[1]);
  not not_15 (not_15_out, X);
  not not_16 (not_16_out, register_1_q[0]);
  not not_17 (not_17_out, register_1_q[3]);
  not not_18 (not_18_out, register_1_q[1]);
  not not_19 (not_19_out, register_1_q[0]);
  not not_20 (not_20_out, register_1_q[3]);
  not not_21 (not_21_out, register_1_q[1]);
  not not_22 (not_22_out, register_1_q[2]);
  not not_23 (not_23_out, X);
  not not_24 (not_24_out, register_1_q[1]);
  not not_25 (not_25_out, register_1_q[0]);
  not not_26 (not_26_out, register_1_q[1]);
  not not_27 (not_27_out, X);
  not not_28 (not_28_out, register_1_q[3]);
  not not_29 (not_29_out, register_1_q[1]);
  not not_30 (not_30_out, register_1_q[0]);
  not not_31 (not_31_out, register_1_q[3]);
  not not_32 (not_32_out, register_1_q[1]);
  not not_33 (not_33_out, register_1_q[2]);
  not not_34 (not_34_out, X);
  not not_35 (not_35_out, register_1_q[3]);
  not not_36 (not_36_out, register_1_q[1]);
  not not_37 (not_37_out, register_1_q[3]);
  not not_38 (not_38_out, register_1_q[0]);
  not not_39 (not_39_out, register_1_q[1]);
  not not_40 (not_40_out, register_1_q[0]);
  not not_41 (not_41_out, register_1_q[3]);
  not not_42 (not_42_out, register_1_q[1]);
  not not_43 (not_43_out, register_1_q[2]);
  not not_44 (not_44_out, X);
  not not_45 (not_45_out, register_1_q[2]);
  not not_46 (not_46_out, X);
  not not_47 (not_47_out, register_1_q[2]);
  not not_48 (not_48_out, register_1_q[1]);
  not not_49 (not_49_out, register_1_q[2]);
  not not_50 (not_50_out, register_1_q[1]);
  not not_51 (not_51_out, X);
  not not_52 (not_52_out, register_1_q[0]);
  not not_53 (not_53_out, register_1_q[2]);
  not not_54 (not_54_out, register_1_q[1]);
  not not_55 (not_55_out, register_1_q[0]);
  not not_56 (not_56_out, register_1_q[2]);
  not not_57 (not_57_out, register_1_q[1]);
  not not_58 (not_58_out, X);
  not not_59 (not_59_out, register_1_q[3]);
  not not_60 (not_60_out, register_1_q[1]);
  not not_61 (not_61_out, register_1_q[0]);
  not not_62 (not_62_out, register_1_q[3]);
  not not_63 (not_63_out, register_1_q[1]);
  not not_64 (not_64_out, register_1_q[2]);
  not not_65 (not_65_out, X);
  not not_66 (not_66_out, register_1_q[3]);
  not not_67 (not_67_out, register_1_q[1]);
  not not_68 (not_68_out, register_1_q[0]);
  not not_69 (not_69_out, register_1_q[2]);
  not not_70 (not_70_out, X);
  not not_71 (not_71_out, register_1_q[2]);
  not not_72 (not_72_out, register_1_q[1]);
  not not_73 (not_73_out, register_1_q[0]);
  not not_74 (not_74_out, register_1_q[2]);
  not not_75 (not_75_out, register_1_q[1]);
  not not_76 (not_76_out, X);
  not not_77 (not_77_out, register_1_q[2]);
  not not_78 (not_78_out, register_1_q[1]);
  not not_79 (not_79_out, register_1_q[0]);
  not not_80 (not_80_out, register_1_q[1]);
  not not_81 (not_81_out, register_1_q[4]);
  not not_82 (not_82_out, X);
  not not_83 (not_83_out, register_1_q[3]);
  not not_84 (not_84_out, X);
  not not_85 (not_85_out, register_1_q[1]);
  not not_86 (not_86_out, register_1_q[0]);
  not not_87 (not_87_out, register_1_q[3]);
  not not_88 (not_88_out, register_1_q[2]);
  not not_89 (not_89_out, register_1_q[1]);
  not not_90 (not_90_out, register_1_q[1]);
  not not_91 (not_91_out, register_1_q[0]);
  and and_1 (and_1_out, register_1_q[3], register_1_q[2], register_1_q[1], register_1_q[0], not_1_out);
  and and_2 (and_2_out, register_1_q[4], not_2_out);
  and and_3 (and_3_out, register_1_q[4], not_3_out);
  and and_4 (and_4_out, register_1_q[4], X);
  and and_5 (and_5_out, not_4_out, register_1_q[2], register_1_q[1], register_1_q[0], not_5_out);
  and and_6 (and_6_out, register_1_q[3], not_6_out);
  and and_7 (and_7_out, register_1_q[3], not_7_out);
  and and_8 (and_8_out, register_1_q[3], not_8_out);
  and and_9 (and_9_out, register_1_q[3], X);
  and and_10 (and_10_out, not_9_out, not_10_out, register_1_q[1], register_1_q[0], not_11_out);
  and and_11 (and_11_out, register_1_q[2], not_12_out);
  and and_12 (and_12_out, register_1_q[2], not_13_out);
  and and_13 (and_13_out, register_1_q[2], X);
  and and_14 (and_14_out, not_14_out, register_1_q[0], not_15_out);
  and and_15 (and_15_out, register_1_q[1], not_16_out);
  and and_16 (and_16_out, register_1_q[1], X);
  and and_17 (and_17_out, not_17_out, not_18_out, not_19_out);
  and and_18 (and_18_out, not_20_out, not_21_out, X);
  and and_19 (and_19_out, not_22_out, register_1_q[1], register_1_q[0], not_23_out);
  and and_20 (and_20_out, register_1_q[2], not_24_out, not_25_out);
  and and_21 (and_21_out, register_1_q[2], not_26_out, X);
  and and_22 (and_22_out, register_1_q[3], register_1_q[1], register_1_q[0], not_27_out);
  and and_23 (and_23_out, not_28_out, not_29_out, not_30_out);
  and and_24 (and_24_out, not_31_out, not_32_out, X);
  and and_25 (and_25_out, not_33_out, register_1_q[1], register_1_q[0], not_34_out);
  and and_26 (and_26_out, not_35_out, register_1_q[2], not_36_out);
  and and_27 (and_27_out, not_37_out, register_1_q[2], not_38_out);
  and and_28 (and_28_out, register_1_q[2], not_39_out, not_40_out);
  and and_29 (and_29_out, not_41_out, register_1_q[2], X);
  and and_30 (and_30_out, register_1_q[2], not_42_out, X);
  and and_31 (and_31_out, register_1_q[3], not_43_out, register_1_q[0], not_44_out);
  and and_32 (and_32_out, register_1_q[3], not_45_out, register_1_q[1]);
  and and_33 (and_33_out, register_1_q[3], register_1_q[1], register_1_q[0], not_46_out);
  and and_34 (and_34_out, not_47_out, not_48_out);
  and and_35 (and_35_out, not_49_out, X);
  and and_36 (and_36_out, not_50_out, register_1_q[0], not_51_out);
  and and_37 (and_37_out, register_1_q[1], not_52_out);
  and and_38 (and_38_out, register_1_q[2], register_1_q[1]);
  not not_92 (not_92_out, register_1_q[3]);
  and and_39 (and_39_out, not_53_out, not_54_out, not_55_out);
  and and_40 (and_40_out, not_56_out, not_57_out, X);
  and and_41 (and_41_out, register_1_q[2], register_1_q[0], not_58_out);
  and and_42 (and_42_out, register_1_q[2], register_1_q[1]);
  and and_43 (and_43_out, not_59_out, not_60_out, not_61_out);
  and and_44 (and_44_out, not_62_out, not_63_out, X);
  and and_45 (and_45_out, not_64_out, register_1_q[1], register_1_q[0], not_65_out);
  and and_46 (and_46_out, not_66_out, register_1_q[2], not_67_out);
  and and_47 (and_47_out, register_1_q[2], not_68_out);
  and and_48 (and_48_out, register_1_q[2], X);
  and and_49 (and_49_out, register_1_q[3], not_69_out, register_1_q[0], not_70_out);
  and and_50 (and_50_out, register_1_q[3], register_1_q[1]);
  and and_51 (and_51_out, not_71_out, not_72_out, not_73_out);
  and and_52 (and_52_out, not_74_out, not_75_out, X);
  and and_53 (and_53_out, register_1_q[2], register_1_q[1], register_1_q[0], not_76_out);
  and and_54 (and_54_out, register_1_q[3], not_77_out);
  and and_55 (and_55_out, register_1_q[3], not_78_out, not_79_out);
  and and_56 (and_56_out, register_1_q[3], not_80_out, X);
  and and_57 (and_57_out, not_81_out, register_1_q[1], register_1_q[0], not_82_out);
  and and_58 (and_58_out, not_83_out, register_1_q[2], not_84_out);
  and and_59 (and_59_out, register_1_q[2], not_85_out, not_86_out);
  and and_60 (and_60_out, not_87_out, register_1_q[2], register_1_q[1]);
  and and_61 (and_61_out, register_1_q[3], not_88_out);
  and and_62 (and_62_out, register_1_q[3], not_89_out, X);
  and and_63 (and_63_out, register_1_q[4], not_90_out);
  and and_64 (and_64_out, register_1_q[4], not_91_out);
  and and_65 (and_65_out, register_1_q[4], X);
  or or_1 (or_4_out[4], and_1_out, and_2_out, and_3_out, and_4_out);
  or or_2 (or_4_out[3], and_5_out, and_6_out, and_7_out, and_8_out, and_9_out);
  or or_3 (or_4_out[2], and_10_out, and_11_out, and_12_out, and_13_out);
  or or_4 (or_4_out[1], and_14_out, and_15_out, and_16_out);
  or or_5 (X6, and_17_out, and_18_out, and_19_out, and_20_out, and_21_out, and_22_out);
  or or_6 (X4, and_34_out, and_35_out, and_36_out, and_37_out, and_38_out, register_1_q[3], register_1_q[4]);
  or or_7 (X3, not_92_out, and_39_out, and_40_out, and_41_out, and_42_out);
  or or_8 (X1, and_51_out, and_52_out, and_53_out, and_54_out, and_55_out, and_56_out, register_1_q[4]);
  or or_9 (X5, and_23_out, and_24_out, and_25_out, and_26_out, and_27_out, and_28_out, and_29_out, and_30_out, and_31_out, and_32_out, and_33_out, register_1_q[4]);
  or or_10 (X2, and_43_out, and_44_out, and_45_out, and_46_out, and_47_out, and_48_out, and_49_out, and_50_out, register_1_q[4]);
  or or_11 (X0, and_57_out, and_58_out, and_59_out, and_60_out, and_61_out, and_62_out, and_63_out, and_64_out, and_65_out);
endmodule
