// Logisim project CONTROL_UNİT.circ as structural Verilog: 2 circuits, main circuit main
module main (
  input  CLK,
  input  S,
  input  B,
  input  E,
  input  D,
  input  G,
  input  L,
  input  H,
  input  R,
  output TTY_CLEAR_SIGNAL,
  output A_SIGNAL,
  output C_SIGNAL,
  output F_SIGNAL
);

  wire and_1_out, and_2_out, and_3_out, and_4_out, and_5_out, and_6_out, and_7_out, and_8_out, and_9_out,
       and_10_out, and_11_out, and_12_out, and_13_out, and_14_out, and_15_out, and_16_out;
  wire [2:0] or_3_out, register_1_q;

  and and_1 (and_1_out, ~D, ~R, ~register_1_q[2], register_1_q[1], register_1_q[0]);  // AND_Gate
  and and_2 (and_2_out, ~G, ~R, register_1_q[2], ~register_1_q[1], ~register_1_q[0]);  // AND_Gate
  and and_3 (and_3_out, G, ~R, register_1_q[2], ~register_1_q[1], ~register_1_q[0]);  // AND_Gate
  and and_4 (and_4_out, H, ~R, register_1_q[2], ~register_1_q[1], register_1_q[0]);  // AND_Gate
  and and_5 (and_5_out, ~R, register_1_q[2], register_1_q[1], ~register_1_q[0]);  // AND_Gate
  and and_6 (and_6_out, B, ~R, ~register_1_q[2], ~register_1_q[1], register_1_q[0]);  // AND_Gate
  and and_7 (and_7_out, ~R, ~register_1_q[2], register_1_q[1], ~register_1_q[0]);  // AND_Gate
  and and_8 (and_8_out, D, ~R, ~register_1_q[2], register_1_q[1], register_1_q[0]);  // AND_Gate
  and and_9 (and_9_out, G, L, ~R, register_1_q[2], ~register_1_q[1], ~register_1_q[0]);  // AND_Gate
  and and_10 (and_10_out, ~R, register_1_q[2], ~register_1_q[1], register_1_q[0]);  // AND_Gate
  and and_11 (and_11_out, ~R, register_1_q[2], register_1_q[1], ~register_1_q[0]);  // AND_Gate
  and and_12 (and_12_out, S, ~R, ~register_1_q[2], ~register_1_q[1], ~register_1_q[0]);  // AND_Gate
  and and_13 (and_13_out, ~B, ~R, ~register_1_q[2], ~register_1_q[1], register_1_q[0]);  // AND_Gate
  and and_14 (and_14_out, E, ~R, ~register_1_q[2], register_1_q[1], ~register_1_q[0]);  // AND_Gate
  and and_15 (and_15_out, D, ~R, ~register_1_q[2], register_1_q[1], register_1_q[0]);  // AND_Gate
  and and_16 (and_16_out, G, ~L, ~R, register_1_q[2], ~register_1_q[1], ~register_1_q[0]);  // AND_Gate
  Main main_1 (
    .S2(register_1_q[2]), .S1(register_1_q[1]), .S0(register_1_q[0]), .TTY_CLEAR_SIGNAL(TTY_CLEAR_SIGNAL),
    .A_SIGNAL(A_SIGNAL), .C_SIGNAL(C_SIGNAL), .F_SIGNAL(F_SIGNAL));
  Register #(.width(3)) register_1 (.D(or_3_out), .Q(register_1_q), .clk(CLK));  // open: en, clr
  or or_1 (or_3_out[2], and_1_out, and_2_out, and_3_out, and_4_out, and_5_out);
  or or_2 (or_3_out[1], and_6_out, and_7_out, and_8_out, and_9_out, and_10_out, and_11_out);
  or or_3 (or_3_out[0], and_12_out, and_13_out, and_14_out, and_15_out, and_16_out);
endmodule

module Main (
  input  S2,
  input  S1,
  input  S0,
  output TTY_CLEAR_SIGNAL,
  output A_SIGNAL,
  output C_SIGNAL,
  output F_SIGNAL
);

  wire and_1_out, and_2_out, not_1_out, not_2_out, not_3_out, not_4_out, not_5_out, not_6_out, not_7_out,
       not_8_out, not_9_out;

  not not_1 (not_1_out, S2);
  not not_2 (not_2_out, S1);
  not not_3 (not_3_out, S0);
  not not_4 (not_4_out, S2);
  not not_5 (not_5_out, S1);
  not not_6 (not_6_out, S2);
  not not_7 (not_7_out, S0);
  not not_8 (not_8_out, S1);
  not not_9 (not_9_out, S0);
  and and_1 (and_1_out, not_1_out, not_2_out, not_3_out);
  and and_2 (and_2_out, S1, S0);
  and A (A_SIGNAL, not_4_out, not_5_out, S0);
  and C (C_SIGNAL, not_6_out, S1, not_7_out);
  and F (F_SIGNAL, S2, not_8_out, not_9_out);
  or TTY_CLEAR (TTY_CLEAR_SIGNAL, and_1_out, and_2_out);
endmodule
