// Logisim project Datapath.circ as structural Verilog: 1 circuit, main circuit main
module main (
  input  A_SIGNAL,
  input  R_SIGNAL,
  input  A,
  input  I,
  input  B,
  input  J,
  input  C,
  input  K,
  input  D,
  input  L,
  input  E,
  input  M,
  input  F,
  input  N,
  input  G,
  input  O,
  input  H,
  input  P,
  input  Q,
  input  Y,
  input  R,
  input  Z,
  input  S,
  input  T,
  input  U,
  input  V,
  input  w,
  input  X,
  input  C_SIGNAL,
  input  F_SIGNAL,
  input  TTY_SIGNAL,
  input  CLK,
  output X0,
  output X1,
  output X2,
  output X3,
  output [6:0] _1,
  output [6:0] _5,
  output X6,
  output X5,
  output X4,
  output [6:0] _2,
  output [6:0] _6,
  output [6:0] _3,
  output [6:0] _7,
  output [6:0] _4,
  output [6:0] _8,
  output [6:0] TTY_DATA,
  output TTY_CLK,
  output B_output,
  output TTY_ENABLE,
  output TTY_CLEAR,
  output E_OUTPUT,
  output L_output,
  output G_output,
  output HM_output,
  output D_SIGNAL
);

  wire comparator_10_eq, comparator_11_eq, comparator_12_eq, comparator_13_eq, comparator_14_eq,
       comparator_15_eq, comparator_16_eq, comparator_17_eq, multiplexer_9_out, multiplexer_10_out,
       multiplexer_11_out, multiplexer_12_out, multiplexer_13_out, multiplexer_14_out, multiplexer_15_out,
       multiplexer_16_out, not_9_out, not_10_out, not_16_out, not_17_out, not_18_out, not_19_out, not_20_out,
       not_21_out, not_22_out, not_23_out, not_30_out, not_31_out, or_2_out, register_9_q, register_10_q,
       register_11_q, register_12_q, register_13_q, register_14_q, register_15_q, register_16_q,
       register_17_q;
  wire [2:0] counter_1_q;
  wire [6:0] main_2_character, multiplexer_1_out, multiplexer_2_out, multiplexer_3_out, multiplexer_4_out,
       multiplexer_5_out, multiplexer_6_out, multiplexer_7_out, multiplexer_8_out, multiplexer_17_out,
       multiplexer_18_out, multiplexer_19_out, multiplexer_20_out, multiplexer_21_out, multiplexer_22_out,
       multiplexer_23_out, multiplexer_24_out, not_24_out, not_26_out, register_1_q, register_2_q,
       register_3_q, register_4_q, register_5_q, register_6_q, register_7_q, register_8_q;
  wire [7:0] comparator_1_eq, not_5_out;

  not not_1 (not_5_out[7], 1'b1);
  not not_2 (not_5_out[5], 1'b1);
  not not_3 (not_5_out[3], 1'b1);
  not not_4 (not_5_out[4], 1'b1);
  not not_5 (not_5_out[0], 1'b1);
  not not_6 (not_5_out[2], 1'b1);
  not not_7 (not_5_out[1], 1'b1);
  not not_8 (not_5_out[6], 1'b1);
  not not_9 (not_9_out, 1'b1);
  Rand_Rom_and_7_Seg_Output_main main_1 (
    ._0_SIGNAL(not_9_out), .CLK(CLK), .A_STATE_2_INP_SIGNAL(A_SIGNAL), .R_RESET(R_SIGNAL),
    .\_0_8_BİT (not_5_out), .C7(_1), .C6(_2), .C5(_3), .C4(_4), .C3(_5), .C2(_6), .C1(_7), .C0(_8), .X6(X6),
    .X5(X5), .X4(X4), .X3(X3), .X2(X2), .X1(X1), .X0(X0), .B_STATE_2_OUTPUT(B_output));
  KEYBOARD_main main_2 (
    .A(A), .I(I), .B(B), .J(J), .C(C), .K(K), .D(D), .L(L), .E(E), .M(M), .F(F), .N(N), .G(G), .O(O), .H(H),
    .P(P), .Q(Q), .Y(Y), .R(R), .Z(Z), .S(S), .T(T), .U(U), .V(V), .w(w), .X(X), .C_SIGNAL(C_SIGNAL),
    .R_SIGNAL(R_SIGNAL), .CHARACTER(main_2_character), .E_2(E_OUTPUT), .CLK(CLK));
  or or_1 (D_SIGNAL, A, I, B, J, C, K, D, L, E, M, F, N, G, O, H, P, Q, Y, R, S, U, w, Z, T, V, X);
  Comparator #(.width(7), .mode("unsigned")) comparator_1 (
    .a(_1), .b(main_2_character), .eq(comparator_1_eq[0]));  // open: gt, lt
  Comparator #(.width(7), .mode("unsigned")) comparator_2 (
    .a(_2), .b(main_2_character), .eq(comparator_1_eq[1]));  // open: gt, lt
  Comparator #(.width(7), .mode("unsigned")) comparator_3 (
    .a(_3), .b(main_2_character), .eq(comparator_1_eq[2]));  // open: gt, lt
  Comparator #(.width(7), .mode("unsigned")) comparator_4 (
    .a(_4), .b(main_2_character), .eq(comparator_1_eq[3]));  // open: gt, lt
  Comparator #(.width(7), .mode("unsigned")) comparator_5 (
    .a(_5), .b(main_2_character), .eq(comparator_1_eq[4]));  // open: gt, lt
  Comparator #(.width(7), .mode("unsigned")) comparator_6 (
    .a(_6), .b(main_2_character), .eq(comparator_1_eq[5]));  // open: gt, lt
  Comparator #(.width(7), .mode("unsigned")) comparator_7 (
    .a(_7), .b(main_2_character), .eq(comparator_1_eq[6]));  // open: gt, lt
  Comparator #(.width(7), .mode("unsigned")) comparator_8 (
    .a(_8), .b(main_2_character), .eq(comparator_1_eq[7]));  // open: gt, lt
  Counter #(.width(3), .max('h7)) counter_1 (
    .Q(counter_1_q), .clk(CLK), .clr(not_10_out));  // open: load, D, count, carry
  not not_10 (not_10_out, F_SIGNAL);
  Comparator #(.width(3), .mode("unsigned")) comparator_9 (.a(counter_1_q), .b(3'b111), .eq(G_output));  // open: gt, lt
  Multiplexer #(.width(7)) multiplexer_1 (
    .in0(_1), .in1(not_24_out), .out(multiplexer_1_out), .sel(R_SIGNAL));  // open: en
  Multiplexer #(.width(7)) multiplexer_2 (
    .in0(_2), .in1(not_24_out), .out(multiplexer_2_out), .sel(R_SIGNAL));  // open: en
  Multiplexer #(.width(7)) multiplexer_3 (
    .in0(_3), .in1(not_24_out), .out(multiplexer_3_out), .sel(R_SIGNAL));  // open: en
  Multiplexer #(.width(7)) multiplexer_4 (
    .in0(_4), .in1(not_24_out), .out(multiplexer_4_out), .sel(R_SIGNAL));  // open: en
  Multiplexer #(.width(7)) multiplexer_5 (
    .in0(_5), .in1(not_24_out), .out(multiplexer_5_out), .sel(R_SIGNAL));  // open: en
  Multiplexer #(.width(7)) multiplexer_6 (
    .in0(_6), .in1(not_24_out), .out(multiplexer_6_out), .sel(R_SIGNAL));  // open: en
  Multiplexer #(.width(7)) multiplexer_7 (
    .in0(_7), .in1(not_24_out), .out(multiplexer_7_out), .sel(R_SIGNAL));  // open: en
  Multiplexer #(.width(7)) multiplexer_8 (
    .in0(_8), .in1(not_24_out), .out(multiplexer_8_out), .sel(R_SIGNAL));  // open: en
  Multiplexer multiplexer_9 (
    .in0(comparator_1_eq[0]), .in1(R_SIGNAL), .out(multiplexer_9_out), .sel(R_SIGNAL));  // open: en
  Multiplexer multiplexer_10 (
    .in0(comparator_1_eq[1]), .in1(R_SIGNAL), .out(multiplexer_10_out), .sel(R_SIGNAL));  // open: en
  Multiplexer multiplexer_11 (
    .in0(comparator_1_eq[2]), .in1(R_SIGNAL), .out(multiplexer_11_out), .sel(R_SIGNAL));  // open: en
  Multiplexer multiplexer_12 (
    .in0(comparator_1_eq[3]), .in1(R_SIGNAL), .out(multiplexer_12_out), .sel(R_SIGNAL));  // open: en
  Multiplexer multiplexer_13 (
    .in0(comparator_1_eq[4]), .in1(R_SIGNAL), .out(multiplexer_13_out), .sel(R_SIGNAL));  // open: en
  Multiplexer multiplexer_14 (
    .in0(comparator_1_eq[5]), .in1(R_SIGNAL), .out(multiplexer_14_out), .sel(R_SIGNAL));  // open: en
  Multiplexer multiplexer_15 (
    .in0(comparator_1_eq[6]), .in1(R_SIGNAL), .out(multiplexer_15_out), .sel(R_SIGNAL));  // open: en
  Multiplexer multiplexer_16 (
    .in0(comparator_1_eq[7]), .in1(R_SIGNAL), .out(multiplexer_16_out), .sel(R_SIGNAL));  // open: en
  Register #(.width(7)) register_1 (
    .D(multiplexer_1_out), .en(multiplexer_9_out), .Q(register_1_q), .clk(CLK), .clr(R_SIGNAL));
  Register #(.width(7)) register_2 (
    .D(multiplexer_2_out), .en(multiplexer_10_out), .Q(register_2_q), .clk(CLK), .clr(R_SIGNAL));
  Register #(.width(7)) register_3 (
    .D(multiplexer_3_out), .en(multiplexer_11_out), .Q(register_3_q), .clk(CLK), .clr(R_SIGNAL));
  Register #(.width(7)) register_4 (
    .D(multiplexer_4_out), .en(multiplexer_12_out), .Q(register_4_q), .clk(CLK), .clr(R_SIGNAL));
  Register #(.width(7)) register_5 (
    .D(multiplexer_5_out), .en(multiplexer_13_out), .Q(register_5_q), .clk(CLK), .clr(R_SIGNAL));
  Register #(.width(7)) register_6 (
    .D(multiplexer_6_out), .en(multiplexer_14_out), .Q(register_6_q), .clk(CLK), .clr(R_SIGNAL));
  Register #(.width(7)) register_7 (
    .D(multiplexer_7_out), .en(multiplexer_15_out), .Q(register_7_q), .clk(CLK), .clr(R_SIGNAL));
  Register #(.width(7)) register_8 (
    .D(multiplexer_8_out), .en(multiplexer_16_out), .Q(register_8_q), .clk(CLK), .clr(R_SIGNAL));
  not not_11 (not_24_out[5], 1'b1);
  not not_12 (not_24_out[4], 1'b1);
  not not_13 (not_24_out[3], 1'b1);
  not not_14 (not_24_out[6], 1'b1);
  not not_15 (not_24_out[2], 1'b1);
  Comparator #(.width(7), .mode("unsigned")) comparator_10 (
    .a(register_1_q), .b(not_24_out), .eq(comparator_10_eq));  // open: gt, lt
  not not_16 (not_16_out, comparator_10_eq);
  Comparator #(.width(7), .mode("unsigned")) comparator_11 (
    .a(register_2_q), .b(not_24_out), .eq(comparator_11_eq));  // open: gt, lt
  not not_17 (not_17_out, comparator_11_eq);
  not not_18 (not_18_out, comparator_12_eq);
  Comparator #(.width(7), .mode("unsigned")) comparator_12 (
    .a(register_3_q), .b(not_24_out), .eq(comparator_12_eq));  // open: gt, lt
  Comparator #(.width(7), .mode("unsigned")) comparator_13 (
    .a(register_4_q), .b(not_24_out), .eq(comparator_13_eq));  // open: gt, lt
  not not_19 (not_19_out, comparator_13_eq);
  not not_20 (not_20_out, comparator_14_eq);
  Comparator #(.width(7), .mode("unsigned")) comparator_14 (
    .a(register_5_q), .b(not_24_out), .eq(comparator_14_eq));  // open: gt, lt
  not not_21 (not_21_out, comparator_15_eq);
  Comparator #(.width(7), .mode("unsigned")) comparator_15 (
    .a(register_6_q), .b(not_24_out), .eq(comparator_15_eq));  // open: gt, lt
  not not_22 (not_22_out, comparator_16_eq);
  Comparator #(.width(7), .mode("unsigned")) comparator_16 (
    .a(register_7_q), .b(not_24_out), .eq(comparator_16_eq));  // open: gt, lt
  not not_23 (not_23_out, comparator_17_eq);
  Comparator #(.width(7), .mode("unsigned")) comparator_17 (
    .a(register_8_q), .b(not_24_out), .eq(comparator_17_eq));  // open: gt, lt
  not not_24 (not_24_out[0], 1'b1);
  not not_25 (not_24_out[1], 1'b1);
  not not_26 (not_26_out[0], 1'b1);
  not not_27 (not_26_out[6], 1'b1);
  not not_28 (not_26_out[4], 1'b1);
  not not_29 (not_26_out[2], 1'b1);
  Multiplexer #(.width(7)) multiplexer_17 (
    .in0({not_26_out[6], 1'b1, not_26_out[4], 1'b1, not_26_out[2], 1'b1, not_26_out[0]}), .in1(_1),
    .out(multiplexer_17_out), .sel(not_16_out));  // open: en
  Multiplexer #(.width(7)) multiplexer_18 (
    .in0({not_26_out[6], 1'b1, not_26_out[4], 1'b1, not_26_out[2], 1'b1, not_26_out[0]}), .in1(_2),
    .out(multiplexer_18_out), .sel(not_17_out));  // open: en
  Multiplexer #(.width(7)) multiplexer_19 (
    .in0({not_26_out[6], 1'b1, not_26_out[4], 1'b1, not_26_out[2], 1'b1, not_26_out[0]}), .in1(_3),
    .out(multiplexer_19_out), .sel(not_18_out));  // open: en
  Multiplexer #(.width(7)) multiplexer_20 (
    .in0({not_26_out[6], 1'b1, not_26_out[4], 1'b1, not_26_out[2], 1'b1, not_26_out[0]}), .in1(_4),
    .out(multiplexer_20_out), .sel(not_19_out));  // open: en
  Multiplexer #(.width(7)) multiplexer_21 (
    .in0({not_26_out[6], 1'b1, not_26_out[4], 1'b1, not_26_out[2], 1'b1, not_26_out[0]}), .in1(_5),
    .out(multiplexer_21_out), .sel(not_20_out));  // open: en
  Multiplexer #(.width(7)) multiplexer_22 (
    .in0({not_26_out[6], 1'b1, not_26_out[4], 1'b1, not_26_out[2], 1'b1, not_26_out[0]}), .in1(_6),
    .out(multiplexer_22_out), .sel(not_21_out));  // open: en
  Multiplexer #(.width(7)) multiplexer_23 (
    .in0({not_26_out[6], 1'b1, not_26_out[4], 1'b1, not_26_out[2], 1'b1, not_26_out[0]}), .in1(_7),
    .out(multiplexer_23_out), .sel(not_22_out));  // open: en
  Multiplexer #(.width(7)) multiplexer_24 (
    .in0({not_26_out[6], 1'b1, not_26_out[4], 1'b1, not_26_out[2], 1'b1, not_26_out[0]}), .in1(_8),
    .out(multiplexer_24_out), .sel(not_23_out));  // open: en
  Multiplexer #(.select(3), .width(7)) multiplexer_25 (
    .in0(multiplexer_17_out), .in1(multiplexer_18_out), .in2(multiplexer_19_out), .in3(multiplexer_20_out),
    .in4(multiplexer_21_out), .in5(multiplexer_22_out), .in6(multiplexer_23_out), .in7(multiplexer_24_out),
    .out(TTY_DATA), .sel(counter_1_q));  // open: en
  Register #(.width(1)) register_9 (
    .D(comparator_1_eq[0]), .en(comparator_1_eq[0]), .Q(register_9_q), .clk(CLK), .clr(R_SIGNAL));
  Register #(.width(1)) register_10 (
    .D(comparator_1_eq[1]), .en(comparator_1_eq[1]), .Q(register_10_q), .clk(CLK), .clr(R_SIGNAL));
  Register #(.width(1)) register_11 (
    .D(comparator_1_eq[3]), .en(comparator_1_eq[3]), .Q(register_11_q), .clk(CLK), .clr(R_SIGNAL));
  Register #(.width(1)) register_12 (
    .D(comparator_1_eq[2]), .en(comparator_1_eq[2]), .Q(register_12_q), .clk(CLK), .clr(R_SIGNAL));
  Register #(.width(1)) register_13 (
    .D(comparator_1_eq[4]), .en(comparator_1_eq[4]), .Q(register_13_q), .clk(CLK), .clr(R_SIGNAL));
  Register #(.width(1)) register_14 (
    .D(comparator_1_eq[5]), .en(comparator_1_eq[5]), .Q(register_14_q), .clk(CLK), .clr(R_SIGNAL));
  Register #(.width(1)) register_15 (
    .D(comparator_1_eq[6]), .en(comparator_1_eq[6]), .Q(register_15_q), .clk(CLK), .clr(R_SIGNAL));
  Register #(.width(1)) register_16 (
    .D(comparator_1_eq[7]), .en(comparator_1_eq[7]), .Q(register_16_q), .clk(CLK), .clr(R_SIGNAL));
  and and_1 (L_output, register_9_q, register_10_q, register_11_q, register_12_q, register_13_q, register_14_q, register_15_q, register_16_q);
  or or_2 (or_2_out, comparator_1_eq[0], comparator_1_eq[1], comparator_1_eq[2], comparator_1_eq[3], comparator_1_eq[4], comparator_1_eq[5], comparator_1_eq[6], comparator_1_eq[7]);
  Register #(.width(1)) register_17 (.D(not_30_out), .en(F_SIGNAL), .Q(register_17_q), .clk(CLK), .clr(C_SIGNAL));
  not not_30 (not_30_out, or_2_out);
  not not_31 (not_31_out, 1'b1);
  Multiplexer multiplexer_26 (.in0(register_17_q), .in1(not_31_out), .out(HM_output), .sel(C_SIGNAL));  // open: en

  assign TTY_CLEAR = TTY_SIGNAL;
  assign TTY_CLK = CLK;
  assign TTY_ENABLE = F_SIGNAL;
endmodule
