// Logisim project Hangman.circ as structural Verilog: 1 circuit, main circuit main
module main (
  input  CLK,
  input  R,
  output [6:0] HM5,
  output [6:0] HM4,
  output [6:0] HM3,
  output [6:0] HM2,
  output [6:0] HM1,
  output H
);

  wire [2:0] not_19_out, not_43_out;
  wire [3:0] counter_1_q, not_39_out;
  wire [4:0] not_14_out;
  wire [5:0] not_8_out;
  wire [5:1] not_34_out, not_59_out, not_95_out, not_99_out;
  wire [6:0] not_1_out, not_21_out, not_46_out, not_64_out, not_71_out, not_77_out, not_82_out;
  wire [6:1] not_28_out, not_53_out, not_89_out;

  Counter #(.width(4), .max('hf)) counter_1 (.Q(counter_1_q), .clk(CLK), .clr(R));  // open: load, D, count, carry
  not not_1 (not_1_out[0], 1'b1);
  not not_2 (not_1_out[1], 1'b1);
  not not_3 (not_1_out[2], 1'b1);
  not not_4 (not_1_out[3], 1'b1);
  not not_5 (not_1_out[4], 1'b1);
  not not_6 (not_1_out[5], 1'b1);
  not not_7 (not_1_out[6], 1'b1);
  not not_8 (not_8_out[0], 1'b1);
  not not_9 (not_8_out[1], 1'b1);
  not not_10 (not_8_out[2], 1'b1);
  not not_11 (not_8_out[3], 1'b1);
  not not_12 (not_8_out[4], 1'b1);
  not not_13 (not_8_out[5], 1'b1);
  not not_14 (not_14_out[0], 1'b1);
  not not_15 (not_14_out[1], 1'b1);
  not not_16 (not_14_out[2], 1'b1);
  not not_17 (not_14_out[3], 1'b1);
  not not_18 (not_14_out[4], 1'b1);
  not not_19 (not_19_out[0], 1'b1);
  not not_20 (not_19_out[2], 1'b1);
  not not_21 (not_21_out[0], 1'b1);
  not not_22 (not_21_out[1], 1'b1);
  not not_23 (not_21_out[2], 1'b1);
  not not_24 (not_21_out[3], 1'b1);
  not not_25 (not_21_out[4], 1'b1);
  not not_26 (not_21_out[5], 1'b1);
  not not_27 (not_21_out[6], 1'b1);
  not not_28 (not_28_out[1], 1'b1);
  not not_29 (not_28_out[2], 1'b1);
  not not_30 (not_28_out[3], 1'b1);
  not not_31 (not_28_out[4], 1'b1);
  not not_32 (not_28_out[5], 1'b1);
  not not_33 (not_28_out[6], 1'b1);
  not not_34 (not_34_out[1], 1'b1);
  not not_35 (not_34_out[2], 1'b1);
  not not_36 (not_34_out[3], 1'b1);
  not not_37 (not_34_out[4], 1'b1);
  not not_38 (not_34_out[5], 1'b1);
  not not_39 (not_39_out[0], 1'b1);
  not not_40 (not_39_out[1], 1'b1);
  not not_41 (not_39_out[2], 1'b1);
  not not_42 (not_39_out[3], 1'b1);
  not not_43 (not_43_out[0], 1'b1);
  not not_44 (not_43_out[1], 1'b1);
  not not_45 (not_43_out[2], 1'b1);
  Multiplexer #(.select(4), .width(7)) multiplexer_1 (
    .in0(not_21_out), .in1({not_28_out, 1'b1}), .in2({not_28_out, 1'b1}), .in3({1'b1, not_34_out, 1'b1}),
    .in4({1'b1, not_34_out, 1'b1}), .in5({1'b1, not_34_out, 1'b1}), .in6({1'b1, not_34_out, 1'b1}),
    .in7({1'b1, not_34_out, 1'b1}), .in8({1'b1, not_34_out, 1'b1}), .in9({1'b1, not_34_out, 1'b1}),
    .in10({1'b1, not_34_out, 1'b1}), .out(HM2), .sel(counter_1_q));  // open: in11, in12, in13, in14, in15, en
  Multiplexer #(.select(4), .width(7)) multiplexer_2 (
    .in0(not_1_out), .in1(not_1_out), .in2(not_1_out), .in3({1'b1, not_8_out}), .in4({2'b11, not_14_out}),
    .in5({2'b11, not_14_out}), .in6({2'b11, not_14_out}), .in7({3'b111, not_39_out}),
    .in8({4'b1111, not_43_out}), .in9({4'b1111, not_43_out}), .in10({4'b1111, not_43_out}), .out(HM4),
    .sel(counter_1_q));  // open: in11, in12, in13, in14, in15, en
  Comparator #(.width(4)) comparator_1 (
    .a(counter_1_q), .b({1'b1, not_19_out[2], 1'b1, not_19_out[0]}), .eq(H));  // open: gt, lt
  not not_46 (not_46_out[0], 1'b1);
  not not_47 (not_46_out[1], 1'b1);
  not not_48 (not_46_out[2], 1'b1);
  not not_49 (not_46_out[3], 1'b1);
  not not_50 (not_46_out[4], 1'b1);
  not not_51 (not_46_out[5], 1'b1);
  not not_52 (not_46_out[6], 1'b1);
  not not_53 (not_53_out[1], 1'b1);
  not not_54 (not_53_out[2], 1'b1);
  not not_55 (not_53_out[3], 1'b1);
  not not_56 (not_53_out[4], 1'b1);
  not not_57 (not_53_out[5], 1'b1);
  not not_58 (not_53_out[6], 1'b1);
  not not_59 (not_59_out[1], 1'b1);
  not not_60 (not_59_out[2], 1'b1);
  not not_61 (not_59_out[3], 1'b1);
  not not_62 (not_59_out[4], 1'b1);
  not not_63 (not_59_out[5], 1'b1);
  not not_64 (not_64_out[0], 1'b1);
  not not_65 (not_64_out[1], 1'b1);
  not not_66 (not_64_out[2], 1'b1);
  not not_67 (not_64_out[3], 1'b1);
  not not_68 (not_64_out[4], 1'b1);
  not not_69 (not_64_out[5], 1'b1);
  not not_70 (not_64_out[6], 1'b1);
  not not_71 (not_71_out[0], 1'b1);
  not not_72 (not_71_out[1], 1'b1);
  not not_73 (not_71_out[2], 1'b1);
  not not_74 (not_71_out[3], 1'b1);
  not not_75 (not_71_out[5], 1'b1);
  not not_76 (not_71_out[6], 1'b1);
  not not_77 (not_77_out[0], 1'b1);
  not not_78 (not_77_out[1], 1'b1);
  not not_79 (not_77_out[3], 1'b1);
  not not_80 (not_77_out[5], 1'b1);
  not not_81 (not_77_out[6], 1'b1);
  not not_82 (not_82_out[0], 1'b1);
  not not_83 (not_82_out[1], 1'b1);
  not not_84 (not_82_out[2], 1'b1);
  not not_85 (not_82_out[3], 1'b1);
  not not_86 (not_82_out[4], 1'b1);
  not not_87 (not_82_out[5], 1'b1);
  not not_88 (not_82_out[6], 1'b1);
  not not_89 (not_89_out[1], 1'b1);
  not not_90 (not_89_out[2], 1'b1);
  not not_91 (not_89_out[3], 1'b1);
  not not_92 (not_89_out[4], 1'b1);
  not not_93 (not_89_out[5], 1'b1);
  not not_94 (not_89_out[6], 1'b1);
  not not_95 (not_95_out[1], 1'b1);
  not not_96 (not_95_out[2], 1'b1);
  not not_97 (not_95_out[3], 1'b1);
  not not_98 (not_95_out[5], 1'b1);
  not not_99 (not_99_out[1], 1'b1);
  not not_100 (not_99_out[3], 1'b1);
  not not_101 (not_99_out[5], 1'b1);
  Multiplexer #(.select(4), .width(7)) multiplexer_3 (
    .in0(not_82_out), .in1({not_89_out, 1'b1}), .in2({7{1'b1}}), .in3({7{1'b1}}), .in4({7{1'b1}}),
    .in5({7{1'b1}}), .in6({7{1'b1}}), .in7({7{1'b1}}), .in8({7{1'b1}}), .in9({7{1'b1}}), .in10({7{1'b1}}),
    .out(HM1), .sel(counter_1_q));  // open: in11, in12, in13, in14, in15, en
  Multiplexer #(.select(4), .width(7)) multiplexer_4 (
    .in0(not_46_out), .in1({not_53_out, 1'b1}), .in2({not_53_out, 1'b1}), .in3({1'b1, not_59_out, 1'b1}),
    .in4({1'b1, not_59_out, 1'b1}), .in5({1'b1, not_95_out[5], 1'b1, not_95_out[3:1], 1'b1}),
    .in6({1'b1, not_95_out[5], 1'b1, not_95_out[3:1], 1'b1}),
    .in7({1'b1, not_95_out[5], 1'b1, not_95_out[3:1], 1'b1}),
    .in8({1'b1, not_95_out[5], 1'b1, not_95_out[3:1], 1'b1}),
    .in9({1'b1, not_99_out[5], 1'b1, not_99_out[3], 1'b1, not_99_out[1], 1'b1}),
    .in10({1'b1, not_99_out[5], 1'b1, not_99_out[3], 1'b1, not_99_out[1], 1'b1}), .out(HM3), .sel(counter_1_q));  // open: in11, in12, in13, in14, in15, en
  Multiplexer #(.select(4), .width(7)) multiplexer_5 (
    .in0(not_64_out), .in1(not_64_out), .in2(not_64_out), .in3(not_64_out), .in4(not_64_out),
    .in5(not_64_out), .in6({not_71_out[6:5], 1'b1, not_71_out[3:0]}),
    .in7({not_71_out[6:5], 1'b1, not_71_out[3:0]}), .in8({not_71_out[6:5], 1'b1, not_71_out[3:0]}),
    .in9({not_71_out[6:5], 1'b1, not_71_out[3:0]}),
    .in10({not_77_out[6:5], 1'b1, not_77_out[3], 1'b1, not_77_out[1:0]}), .out(HM5), .sel(counter_1_q));  // open: in11, in12, in13, in14, in15, en
endmodule
