// Logisim project KEYBOARD.circ as structural Verilog: 1 circuit, main circuit main
module main (
  input  A,
  input  I,
  input  B,
  input  J,
  input  C,
  input  K,
  input  D,
  input  L,
  input  E,
  input  M,
  input  F,
  input  N,
  input  G,
  input  O,
  input  H,
  input  P,
  input  Q,
  input  Y,
  input  R,
  input  Z,
  input  S,
  input  R_SIGNAL,
  input  T,
  input  U,
  input  V,
  input  w,
  input  X,
  input  C_SIGNAL,
  input  CLK,
  output [6:0] CHARACTER,
  output E_2
);

  wire comparator_1_eq, multiplexer_27_out, multiplexer_29_out, not_97_out, not_101_out;
  wire [4:0] counter_1_q;
  wire [5:0] not_6_out, not_15_out, not_24_out, not_31_out, not_40_out, not_47_out, not_54_out, not_59_out,
       not_67_out, not_74_out, not_81_out, not_86_out, not_94_out;
  wire [5:1] not_1_out, not_20_out, not_36_out, not_51_out, not_63_out, not_78_out, not_91_out;
  wire [5:2] not_11_out, not_44_out, not_71_out;
  wire [5:3] not_28_out, not_57_out;
  wire [5:4] not_84_out;
  wire [6:0] multiplexer_1_out, multiplexer_2_out, multiplexer_3_out, multiplexer_4_out, multiplexer_5_out,
       multiplexer_6_out, multiplexer_7_out, multiplexer_8_out, multiplexer_9_out, multiplexer_10_out,
       multiplexer_11_out, multiplexer_12_out, multiplexer_13_out, multiplexer_14_out, multiplexer_15_out,
       multiplexer_16_out, multiplexer_17_out, multiplexer_18_out, multiplexer_19_out, multiplexer_20_out,
       multiplexer_21_out, multiplexer_22_out, multiplexer_23_out, multiplexer_24_out, multiplexer_25_out,
       multiplexer_26_out, multiplexer_28_out, not_109_out, not_113_out, register_1_q, register_2_q,
       register_3_q, register_4_q, register_5_q, register_6_q, register_7_q, register_8_q, register_9_q,
       register_10_q, register_11_q, register_12_q, register_13_q, register_14_q, register_15_q,
       register_16_q, register_17_q, register_18_q, register_19_q, register_20_q, register_21_q,
       register_22_q, register_23_q, register_24_q, register_25_q, register_26_q;

  not not_1 (not_1_out[1], 1'b1);
  not not_2 (not_1_out[2], 1'b1);
  not not_3 (not_1_out[3], 1'b1);
  not not_4 (not_1_out[4], 1'b1);
  not not_5 (not_1_out[5], 1'b1);
  not not_6 (not_6_out[0], 1'b1);
  not not_7 (not_6_out[2], 1'b1);
  not not_8 (not_6_out[3], 1'b1);
  not not_9 (not_6_out[4], 1'b1);
  not not_10 (not_6_out[5], 1'b1);
  not not_11 (not_11_out[2], 1'b1);
  not not_12 (not_11_out[3], 1'b1);
  not not_13 (not_11_out[4], 1'b1);
  not not_14 (not_11_out[5], 1'b1);
  not not_15 (not_15_out[0], 1'b1);
  not not_16 (not_15_out[1], 1'b1);
  not not_17 (not_15_out[3], 1'b1);
  not not_18 (not_15_out[4], 1'b1);
  not not_19 (not_15_out[5], 1'b1);
  not not_20 (not_20_out[1], 1'b1);
  not not_21 (not_20_out[3], 1'b1);
  not not_22 (not_20_out[4], 1'b1);
  not not_23 (not_20_out[5], 1'b1);
  not not_24 (not_24_out[0], 1'b1);
  not not_25 (not_24_out[3], 1'b1);
  not not_26 (not_24_out[4], 1'b1);
  not not_27 (not_24_out[5], 1'b1);
  not not_28 (not_28_out[3], 1'b1);
  not not_29 (not_28_out[4], 1'b1);
  not not_30 (not_28_out[5], 1'b1);
  not not_31 (not_31_out[0], 1'b1);
  not not_32 (not_31_out[1], 1'b1);
  not not_33 (not_31_out[2], 1'b1);
  not not_34 (not_31_out[4], 1'b1);
  not not_35 (not_31_out[5], 1'b1);
  not not_36 (not_36_out[1], 1'b1);
  not not_37 (not_36_out[2], 1'b1);
  not not_38 (not_36_out[3], 1'b1);
  not not_39 (not_36_out[5], 1'b1);
  not not_40 (not_40_out[0], 1'b1);
  not not_41 (not_40_out[2], 1'b1);
  not not_42 (not_40_out[3], 1'b1);
  not not_43 (not_40_out[5], 1'b1);
  not not_44 (not_44_out[2], 1'b1);
  not not_45 (not_44_out[3], 1'b1);
  not not_46 (not_44_out[5], 1'b1);
  not not_47 (not_47_out[0], 1'b1);
  not not_48 (not_47_out[1], 1'b1);
  not not_49 (not_47_out[3], 1'b1);
  not not_50 (not_47_out[5], 1'b1);
  not not_51 (not_51_out[1], 1'b1);
  not not_52 (not_51_out[3], 1'b1);
  not not_53 (not_51_out[5], 1'b1);
  not not_54 (not_54_out[0], 1'b1);
  not not_55 (not_54_out[3], 1'b1);
  not not_56 (not_54_out[5], 1'b1);
  not not_57 (not_57_out[3], 1'b1);
  not not_58 (not_57_out[5], 1'b1);
  not not_59 (not_59_out[0], 1'b1);
  not not_60 (not_59_out[1], 1'b1);
  not not_61 (not_59_out[2], 1'b1);
  not not_62 (not_59_out[5], 1'b1);
  Multiplexer #(.width(7)) multiplexer_1 (
    .in0(not_113_out), .in1({1'b1, not_1_out, 1'b1}), .out(multiplexer_1_out), .sel(A));  // open: en
  Multiplexer #(.width(7)) multiplexer_2 (
    .in0(not_113_out), .in1({1'b1, not_6_out[5:2], 1'b1, not_6_out[0]}), .out(multiplexer_2_out), .sel(B));  // open: en
  Multiplexer #(.width(7)) multiplexer_3 (
    .in0(not_113_out), .in1({1'b1, not_11_out, 2'b11}), .out(multiplexer_3_out), .sel(C));  // open: en
  Multiplexer #(.width(7)) multiplexer_4 (
    .in0(not_113_out), .in1({1'b1, not_15_out[5:3], 1'b1, not_15_out[1:0]}), .out(multiplexer_4_out), .sel(D));  // open: en
  Multiplexer #(.width(7)) multiplexer_5 (
    .in0(not_113_out), .in1({1'b1, not_20_out[5:3], 1'b1, not_20_out[1], 1'b1}), .out(multiplexer_5_out),
    .sel(E));  // open: en
  Multiplexer #(.width(7)) multiplexer_6 (
    .in0(not_113_out), .in1({1'b1, not_24_out[5:3], 2'b11, not_24_out[0]}), .out(multiplexer_6_out), .sel(F));  // open: en
  Multiplexer #(.width(7)) multiplexer_7 (
    .in0(not_113_out), .in1({1'b1, not_28_out, 3'b111}), .out(multiplexer_7_out), .sel(G));  // open: en
  Multiplexer #(.width(7)) multiplexer_8 (
    .in0(not_113_out), .in1({1'b1, not_31_out[5:4], 1'b1, not_31_out[2:0]}), .out(multiplexer_8_out), .sel(H));  // open: en
  Multiplexer #(.width(7)) multiplexer_9 (
    .in0(not_113_out), .in1({1'b1, not_36_out[5], 1'b1, not_36_out[3:1], 1'b1}), .out(multiplexer_9_out),
    .sel(Q));  // open: en
  Multiplexer #(.width(7)) multiplexer_10 (
    .in0(not_113_out), .in1({1'b1, not_40_out[5], 1'b1, not_40_out[3:2], 1'b1, not_40_out[0]}),
    .out(multiplexer_10_out), .sel(R));  // open: en
  Multiplexer #(.width(7)) multiplexer_11 (
    .in0(not_113_out), .in1({1'b1, not_44_out[5], 1'b1, not_44_out[3:2], 2'b11}), .out(multiplexer_11_out),
    .sel(S));  // open: en
  Multiplexer #(.width(7)) multiplexer_12 (
    .in0(not_113_out), .in1({1'b1, not_47_out[5], 1'b1, not_47_out[3], 1'b1, not_47_out[1:0]}),
    .out(multiplexer_12_out), .sel(T));  // open: en
  Multiplexer #(.width(7)) multiplexer_13 (
    .in0(not_113_out), .in1({1'b1, not_51_out[5], 1'b1, not_51_out[3], 1'b1, not_51_out[1], 1'b1}),
    .out(multiplexer_13_out), .sel(U));  // open: en
  Multiplexer #(.width(7)) multiplexer_14 (
    .in0(not_113_out), .in1({1'b1, not_54_out[5], 1'b1, not_54_out[3], 2'b11, not_54_out[0]}),
    .out(multiplexer_14_out), .sel(V));  // open: en
  Multiplexer #(.width(7)) multiplexer_15 (
    .in0(not_113_out), .in1({1'b1, not_57_out[5], 1'b1, not_57_out[3], 3'b111}), .out(multiplexer_15_out),
    .sel(w));  // open: en
  Multiplexer #(.width(7)) multiplexer_16 (
    .in0(not_113_out), .in1({1'b1, not_59_out[5], 2'b11, not_59_out[2:0]}), .out(multiplexer_16_out), .sel(X));  // open: en
  Register #(.width(7)) register_1 (.D(multiplexer_1_out), .Q(register_1_q), .clk(CLK));  // open: en, clr
  Register #(.width(7)) register_2 (.D(multiplexer_2_out), .Q(register_2_q), .clk(CLK));  // open: en, clr
  Register #(.width(7)) register_3 (.D(multiplexer_3_out), .Q(register_3_q), .clk(CLK));  // open: en, clr
  Register #(.width(7)) register_4 (.D(multiplexer_4_out), .Q(register_4_q), .clk(CLK));  // open: en, clr
  Register #(.width(7)) register_5 (.D(multiplexer_5_out), .Q(register_5_q), .clk(CLK));  // open: en, clr
  Register #(.width(7)) register_6 (.D(multiplexer_6_out), .Q(register_6_q), .clk(CLK));  // open: en, clr
  Register #(.width(7)) register_7 (.D(multiplexer_7_out), .Q(register_7_q), .clk(CLK));  // open: en, clr
  Register #(.width(7)) register_8 (.D(multiplexer_8_out), .Q(register_8_q), .clk(CLK));  // open: en, clr
  Register #(.width(7)) register_9 (.D(multiplexer_9_out), .Q(register_9_q), .clk(CLK));  // open: en, clr
  Register #(.width(7)) register_10 (.D(multiplexer_10_out), .Q(register_10_q), .clk(CLK));  // open: en, clr
  Register #(.width(7)) register_11 (.D(multiplexer_11_out), .Q(register_11_q), .clk(CLK));  // open: en, clr
  Register #(.width(7)) register_12 (.D(multiplexer_12_out), .Q(register_12_q), .clk(CLK));  // open: en, clr
  Register #(.width(7)) register_13 (.D(multiplexer_13_out), .Q(register_13_q), .clk(CLK));  // open: en, clr
  Register #(.width(7)) register_14 (.D(multiplexer_14_out), .Q(register_14_q), .clk(CLK));  // open: en, clr
  Register #(.width(7)) register_15 (.D(multiplexer_15_out), .Q(register_15_q), .clk(CLK));  // open: en, clr
  Register #(.width(7)) register_16 (.D(multiplexer_16_out), .Q(register_16_q), .clk(CLK));  // open: en, clr
  not not_63 (not_63_out[1], 1'b1);
  not not_64 (not_63_out[2], 1'b1);
  not not_65 (not_63_out[4], 1'b1);
  not not_66 (not_63_out[5], 1'b1);
  not not_67 (not_67_out[0], 1'b1);
  not not_68 (not_67_out[2], 1'b1);
  not not_69 (not_67_out[4], 1'b1);
  not not_70 (not_67_out[5], 1'b1);
  not not_71 (not_71_out[2], 1'b1);
  not not_72 (not_71_out[4], 1'b1);
  not not_73 (not_71_out[5], 1'b1);
  not not_74 (not_74_out[0], 1'b1);
  not not_75 (not_74_out[1], 1'b1);
  not not_76 (not_74_out[4], 1'b1);
  not not_77 (not_74_out[5], 1'b1);
  not not_78 (not_78_out[1], 1'b1);
  not not_79 (not_78_out[4], 1'b1);
  not not_80 (not_78_out[5], 1'b1);
  not not_81 (not_81_out[0], 1'b1);
  not not_82 (not_81_out[4], 1'b1);
  not not_83 (not_81_out[5], 1'b1);
  not not_84 (not_84_out[4], 1'b1);
  not not_85 (not_84_out[5], 1'b1);
  not not_86 (not_86_out[0], 1'b1);
  not not_87 (not_86_out[1], 1'b1);
  not not_88 (not_86_out[2], 1'b1);
  not not_89 (not_86_out[3], 1'b1);
  not not_90 (not_86_out[5], 1'b1);
  not not_91 (not_91_out[1], 1'b1);
  not not_92 (not_91_out[2], 1'b1);
  not not_93 (not_91_out[5], 1'b1);
  not not_94 (not_94_out[0], 1'b1);
  not not_95 (not_94_out[2], 1'b1);
  not not_96 (not_94_out[5], 1'b1);
  Multiplexer #(.width(7)) multiplexer_17 (
    .in0(not_113_out), .in1({1'b1, not_63_out[5:4], 1'b1, not_63_out[2:1], 1'b1}), .out(multiplexer_17_out),
    .sel(I));  // open: en
  Multiplexer #(.width(7)) multiplexer_18 (
    .in0(not_113_out), .in1({1'b1, not_67_out[5:4], 1'b1, not_67_out[2], 1'b1, not_67_out[0]}),
    .out(multiplexer_18_out), .sel(J));  // open: en
  Multiplexer #(.width(7)) multiplexer_19 (
    .in0(not_113_out), .in1({1'b1, not_71_out[5:4], 1'b1, not_71_out[2], 2'b11}), .out(multiplexer_19_out),
    .sel(K));  // open: en
  Multiplexer #(.width(7)) multiplexer_20 (
    .in0(not_113_out), .in1({1'b1, not_74_out[5:4], 2'b11, not_74_out[1:0]}), .out(multiplexer_20_out),
    .sel(L));  // open: en
  Multiplexer #(.width(7)) multiplexer_21 (
    .in0(not_113_out), .in1({1'b1, not_78_out[5:4], 2'b11, not_78_out[1], 1'b1}), .out(multiplexer_21_out),
    .sel(M));  // open: en
  Multiplexer #(.width(7)) multiplexer_22 (
    .in0(not_113_out), .in1({1'b1, not_81_out[5:4], 3'b111, not_81_out[0]}), .out(multiplexer_22_out), .sel(N));  // open: en
  Multiplexer #(.width(7)) multiplexer_23 (
    .in0(not_113_out), .in1({1'b1, not_84_out, 4'b1111}), .out(multiplexer_23_out), .sel(O));  // open: en
  Multiplexer #(.width(7)) multiplexer_24 (
    .in0(not_113_out), .in1({1'b1, not_86_out[5], 1'b1, not_86_out[3:0]}), .out(multiplexer_24_out), .sel(P));  // open: en
  Multiplexer #(.width(7)) multiplexer_25 (
    .in0(not_113_out), .in1({1'b1, not_91_out[5], 2'b11, not_91_out[2:1], 1'b1}), .out(multiplexer_25_out),
    .sel(Y));  // open: en
  Multiplexer #(.width(7)) multiplexer_26 (
    .in0(not_113_out), .in1({1'b1, not_94_out[5], 2'b11, not_94_out[2], 1'b1, not_94_out[0]}),
    .out(multiplexer_26_out), .sel(Z));  // open: en
  Register #(.width(7)) register_17 (.D(multiplexer_17_out), .Q(register_17_q), .clk(CLK));  // open: en, clr
  Register #(.width(7)) register_18 (.D(multiplexer_18_out), .Q(register_18_q), .clk(CLK));  // open: en, clr
  Register #(.width(7)) register_19 (.D(multiplexer_19_out), .Q(register_19_q), .clk(CLK));  // open: en, clr
  Register #(.width(7)) register_20 (.D(multiplexer_20_out), .Q(register_20_q), .clk(CLK));  // open: en, clr
  Register #(.width(7)) register_21 (.D(multiplexer_21_out), .Q(register_21_q), .clk(CLK));  // open: en, clr
  Register #(.width(7)) register_22 (.D(multiplexer_22_out), .Q(register_22_q), .clk(CLK));  // open: en, clr
  Register #(.width(7)) register_23 (.D(multiplexer_23_out), .Q(register_23_q), .clk(CLK));  // open: en, clr
  Register #(.width(7)) register_24 (.D(multiplexer_24_out), .Q(register_24_q), .clk(CLK));  // open: en, clr
  Register #(.width(7)) register_25 (.D(multiplexer_25_out), .Q(register_25_q), .clk(CLK));  // open: en, clr
  Register #(.width(7)) register_26 (.D(multiplexer_26_out), .Q(register_26_q), .clk(CLK));  // open: en, clr
  Counter #(.width(5), .max('h1f)) counter_1 (
    .Q(counter_1_q), .clk(CLK), .clr(multiplexer_27_out));  // open: load, D, count, carry
  Multiplexer multiplexer_27 (
    .in0(not_97_out), .in1(not_101_out), .out(multiplexer_27_out), .sel(R_SIGNAL));  // open: en
  not not_97 (not_97_out, C_SIGNAL);
  Multiplexer #(.select(5), .width(7)) multiplexer_28 (
    .in1(register_1_q), .in2(register_2_q), .in3(register_3_q), .in4(register_4_q), .in5(register_5_q),
    .in6(register_6_q), .in7(register_8_q), .in8(register_17_q), .in9(register_18_q), .in10(register_19_q),
    .in11(register_20_q), .in12(register_21_q), .in13(register_22_q), .in14(register_23_q),
    .in15(register_24_q), .in16(register_9_q), .in17(register_10_q), .in18(register_11_q),
    .in19(register_12_q), .in20(register_13_q), .in21(register_14_q), .in22(register_15_q),
    .in23(register_16_q), .in24(register_25_q), .in25(register_26_q), .in26(register_7_q),
    .out(multiplexer_28_out), .sel(counter_1_q));  // open: in0, in27, in28, in29, in30, in31, en
  not not_98 (not_109_out[6], 1'b1);
  not not_99 (not_109_out[5], 1'b1);
  not not_100 (not_109_out[4], 1'b1);
  not not_101 (not_101_out, R_SIGNAL);
  not not_102 (not_113_out[4], 1'b1);
  not not_103 (not_113_out[1], 1'b1);
  not not_104 (not_113_out[6], 1'b1);
  not not_105 (not_113_out[5], 1'b1);
  not not_106 (not_113_out[2], 1'b1);
  not not_107 (not_113_out[3], 1'b1);
  Multiplexer multiplexer_29 (.in0(E_2), .in1(R_SIGNAL), .out(multiplexer_29_out), .sel(R_SIGNAL));  // open: en
  not not_108 (E_2, comparator_1_eq);
  Comparator #(.width(7), .mode("unsigned")) comparator_1 (
    .a(multiplexer_28_out), .b(not_109_out), .eq(comparator_1_eq));  // open: gt, lt
  not not_109 (not_109_out[0], 1'b1);
  not not_110 (not_109_out[1], 1'b1);
  not not_111 (not_109_out[3], 1'b1);
  not not_112 (not_109_out[2], 1'b1);
  not not_113 (not_113_out[0], 1'b1);
  Register #(.width(7)) register_27 (
    .D(multiplexer_28_out), .en(multiplexer_29_out), .Q(CHARACTER), .clk(CLK));  // open: clr
endmodule
