// Logisim project MAIN.circ as structural Verilog: 1 circuit, main circuit main
// w
module main (
  output [6:0] _1,
  output [6:0] _5,
  output [6:0] _2,
  output [6:0] _6,
  output [6:0] _3,
  output [6:0] _7,
  output [6:0] _4,
  output [6:0] _1_2
);

  wire A_out, B_out, C_out, clock_1_out, D_out, E_out, F_out, G_out, H_out, hex_1_x0, hex_1_x1, hex_1_x2,
       hex_1_x3, hex_1_x4, hex_1_x5, hex_1_x6, hex_2_x0, hex_2_x1, hex_2_x2, hex_2_x3, hex_2_x4, hex_2_x5,
       hex_2_x6, I_out, J_out, K_out, L_out, M_out, main_1_b_output, main_1_d_signal, main_1_e_output,
       main_1_g_output, main_1_hm_output, main_1_l_output, main_1_tty_clear, main_1_tty_clk,
       main_1_tty_enable, main_1_x0, main_1_x1, main_1_x2, main_1_x3, main_1_x4, main_1_x5, main_1_x6,
       main_2_a_signal, main_2_c_signal, main_2_f_signal, main_2_tty_clear_signal, main_3_h, N_out, O_out,
       P_out, Q_out, R_out, RESET_out, S_out, START_out, T_out, U_out, V_out, W_out, X_out, Y_out, Z_out;
  wire [6:0] main_1_tty_data, main_3_hm1, main_3_hm2, main_3_hm3, main_3_hm4, main_3_hm5;

  Button U (.out(U_out));
  Button W (.out(W_out));
  Button X (.out(X_out));
  Button I (.out(I_out));
  Button J (.out(J_out));
  Button K (.out(K_out));
  Button L (.out(L_out));
  Button M (.out(M_out));
  Button N (.out(N_out));
  Button O (.out(O_out));
  Button P (.out(P_out));
  Button Y (.out(Y_out));
  Button Z (.out(Z_out));
  Button T (.out(T_out));
  Button V (.out(V_out));
  Button Q (.out(Q_out));
  Button S (.out(S_out));
  Button R (.out(R_out));
  Button H (.out(H_out));
  Button RESET (.out(RESET_out));
  Button START (.out(START_out));
  Button D (.out(D_out));
  Button G (.out(G_out));
  Button E (.out(E_out));
  Button F (.out(F_out));
  Button A (.out(A_out));
  Button B (.out(B_out));
  Button C (.out(C_out));
  Clock clock_1 (.out(clock_1_out));
  Datapath_main main_1 (
    .A_SIGNAL(main_2_a_signal), .R_SIGNAL(RESET_out), .A(A_out), .I(I_out), .B(B_out), .J(J_out), .C(C_out),
    .K(K_out), .D(D_out), .L(L_out), .E(E_out), .M(M_out), .F(F_out), .N(N_out), .G(G_out), .O(O_out),
    .H(H_out), .P(P_out), .Q(Q_out), .Y(Y_out), .R(R_out), .Z(Z_out), .S(S_out), .T(T_out), .U(U_out),
    .V(V_out), .w(W_out), .X(X_out), .C_SIGNAL(main_2_c_signal), .F_SIGNAL(main_2_f_signal),
    .TTY_SIGNAL(main_2_tty_clear_signal), .CLK(clock_1_out), .X6(main_1_x6), .X5(main_1_x5), .X4(main_1_x4),
    .X0(main_1_x0), .X1(main_1_x1), .X2(main_1_x2), .X3(main_1_x3), ._1(_1), ._5(_5), ._2(_2), ._6(_6),
    ._3(_3), ._7(_7), ._4(_4), ._8(_1_2), .TTY_DATA(main_1_tty_data), .TTY_CLK(main_1_tty_clk),
    .B_output(main_1_b_output), .TTY_ENABLE(main_1_tty_enable), .TTY_CLEAR(main_1_tty_clear),
    .E_OUTPUT(main_1_e_output), .L_output(main_1_l_output), .G_output(main_1_g_output),
    .HM_output(main_1_hm_output), .D_SIGNAL(main_1_d_signal));
  \CONTROL_UNİT_main  main_2 (
    .CLK(clock_1_out), .S(START_out), .B(main_1_b_output), .E(main_1_e_output), .D(main_1_d_signal),
    .G(main_1_g_output), .L(main_1_l_output), .H(main_3_h), .R(RESET_out),
    .TTY_CLEAR_SIGNAL(main_2_tty_clear_signal), .A_SIGNAL(main_2_a_signal), .C_SIGNAL(main_2_c_signal),
    .F_SIGNAL(main_2_f_signal));
  Hangman_main main_3 (
    .CLK(main_1_hm_output), .R(RESET_out), .HM1(main_3_hm1), .HM2(main_3_hm2), .HM3(main_3_hm3),
    .HM4(main_3_hm4), .HM5(main_3_hm5), .H(main_3_h));
  TTY #(.rows(1), .cols(8)) tty_1 (
    .data(main_1_tty_data), .clk(main_1_tty_clk), .we(main_1_tty_enable), .clr(main_1_tty_clear));
  DotMatrix dotmatrix_1 (.col0(main_3_hm1), .col1(main_3_hm2), .col2(main_3_hm3), .col3(main_3_hm4), .col4(main_3_hm5));
  HEX hex_1 (
    .CLK(clock_1_out), .X(main_3_h), .X6(hex_1_x6), .X5(hex_1_x5), .X4(hex_1_x4), .X3(hex_1_x3),
    .X2(hex_1_x2), .X1(hex_1_x1), .X0(hex_1_x0));
  HEX hex_2 (
    .CLK(clock_1_out), .X(main_1_l_output), .X6(hex_2_x6), .X5(hex_2_x5), .X4(hex_2_x4), .X3(hex_2_x3),
    .X2(hex_2_x2), .X1(hex_2_x1), .X0(hex_2_x0));
  _7_Segment_Display u_7_segment_display_1 (
    .g(main_1_x0), .f(main_1_x1), .a(main_1_x2), .b(main_1_x3), .e(main_1_x6), .d(main_1_x5), .c(main_1_x4));  // open: dp
  _7_Segment_Display u_7_segment_display_2 (
    .g(hex_1_x0), .f(hex_1_x1), .a(hex_1_x2), .b(hex_1_x3), .e(hex_1_x6), .d(hex_1_x5), .c(hex_1_x4));  // open: dp
  _7_Segment_Display u_7_segment_display_3 (
    .g(hex_2_x0), .f(hex_2_x1), .a(hex_2_x2), .b(hex_2_x3), .e(hex_2_x6), .d(hex_2_x5), .c(hex_2_x4));  // open: dp
endmodule
