// Logisim project PROJECT_7_Seg_FSM.circ as structural Verilog: 2 circuits, main circuit HEX_DISPLAY
module HEX_DISPLAY (
  input  CLK,
  input  X,
  input  R,
  output X6,
  output X5,
  output X4,
  output X3,
  output X2,
  output X1,
  output X0
);

  wire and_1_out, and_2_out, and_3_out, and_4_out, and_5_out, and_6_out, and_7_out, and_8_out, and_9_out,
       and_10_out, and_11_out, not_1_out, not_2_out, not_3_out, not_4_out, not_5_out, not_6_out, not_7_out,
       not_8_out, not_9_out, not_10_out, not_11_out, not_12_out, not_13_out, not_14_out, not_15_out,
       not_16_out, not_17_out, not_18_out, not_19_out, not_20_out, not_21_out;
  wire [3:0] or_4_out, register_1_q;

  Register #(.width(4)) register_1 (.D(or_4_out), .Q(register_1_q), .clk(CLK));  // open: en, clr
  not not_1 (not_1_out, R);
  not not_2 (not_2_out, R);
  not not_3 (not_3_out, register_1_q[2]);
  not not_4 (not_4_out, R);
  not not_5 (not_5_out, register_1_q[1]);
  not not_6 (not_6_out, R);
  not not_7 (not_7_out, register_1_q[0]);
  not not_8 (not_8_out, R);
  not not_9 (not_9_out, X);
  not not_10 (not_10_out, R);
  not not_11 (not_11_out, register_1_q[1]);
  not not_12 (not_12_out, R);
  not not_13 (not_13_out, register_1_q[0]);
  not not_14 (not_14_out, R);
  not not_15 (not_15_out, X);
  not not_16 (not_16_out, R);
  not not_17 (not_17_out, register_1_q[3]);
  not not_18 (not_18_out, register_1_q[0]);
  not not_19 (not_19_out, R);
  not not_20 (not_20_out, X);
  not not_21 (not_21_out, R);
  HEX_DISPLAY_OUTPUT hex_display_output_1 (
    .S3(register_1_q[3]), .S2(register_1_q[2]), .S1(register_1_q[1]), .S0(register_1_q[0]), .X6(X6), .X5(X5),
    .X4(X4), .X3(X3), .X2(X2), .X1(X1), .X0(X0));
  and and_1 (and_1_out, register_1_q[2], register_1_q[1], register_1_q[0], X, not_1_out);
  and and_2 (and_2_out, register_1_q[3], not_2_out);
  and and_3 (and_3_out, not_3_out, register_1_q[1], register_1_q[0], X, not_4_out);
  and and_4 (and_4_out, register_1_q[2], not_5_out, not_6_out);
  and and_5 (and_5_out, register_1_q[2], not_7_out, not_8_out);
  and and_6 (and_6_out, register_1_q[2], not_9_out, not_10_out);
  and and_7 (and_7_out, not_11_out, register_1_q[0], X, not_12_out);
  and and_8 (and_8_out, register_1_q[1], not_13_out, not_14_out);
  and and_9 (and_9_out, register_1_q[1], not_15_out, not_16_out);
  and and_10 (and_10_out, not_17_out, not_18_out, X, not_19_out);
  and and_11 (and_11_out, register_1_q[0], not_20_out, not_21_out);
  or or_1 (or_4_out[3], and_1_out, and_2_out);
  or or_2 (or_4_out[2], and_3_out, and_4_out, and_5_out, and_6_out);
  or or_3 (or_4_out[1], and_7_out, and_8_out, and_9_out);
  or or_4 (or_4_out[0], and_10_out, and_11_out);
endmodule

module HEX_DISPLAY_OUTPUT (
  input  S3,
  input  S2,
  input  S1,
  input  S0,
  output X6,
  output X5,
  output X4,
  output X3,
  output X2,
  output X1,
  output X0
);

  wire and_1_out, and_2_out, and_3_out, and_4_out, and_5_out, and_6_out, and_7_out, and_8_out, and_9_out,
       and_10_out, and_11_out, and_12_out, and_13_out, and_14_out, and_15_out, and_16_out, not_1_out,
       not_2_out, not_3_out, not_4_out, not_5_out, not_6_out, not_7_out, not_8_out, not_9_out, not_10_out,
       not_11_out, not_12_out, not_13_out, not_14_out, not_15_out, not_16_out, not_17_out, not_18_out,
       not_19_out, not_20_out, not_21_out;

  not not_1 (not_1_out, S2);
  and and_1 (and_1_out, not_1_out, not_2_out);
  not not_2 (not_2_out, S0);
  and and_2 (and_2_out, S1, not_3_out);
  not not_3 (not_3_out, S0);
  not not_4 (not_4_out, S2);
  and and_3 (and_3_out, not_4_out, not_5_out);
  not not_5 (not_5_out, S0);
  not not_6 (not_6_out, S2);
  and and_4 (and_4_out, not_6_out, S1);
  and and_5 (and_5_out, S1, not_7_out);
  not not_7 (not_7_out, S0);
  not not_8 (not_8_out, S1);
  and and_6 (and_6_out, S2, not_8_out, S0);
  not not_9 (not_9_out, S1);
  or or_1 (X4, not_9_out, S0, S2);
  not not_10 (not_10_out, S2);
  not not_11 (not_11_out, S1);
  and and_7 (and_7_out, not_11_out, not_12_out);
  not not_12 (not_12_out, S0);
  and and_8 (and_8_out, S1, S0);
  not not_13 (not_13_out, S2);
  and and_9 (and_9_out, not_13_out, not_14_out);
  not not_14 (not_14_out, S0);
  and and_10 (and_10_out, S2, S0);
  not not_15 (not_15_out, S1);
  and and_11 (and_11_out, not_15_out, not_16_out);
  not not_16 (not_16_out, S0);
  and and_12 (and_12_out, S2, not_17_out);
  not not_17 (not_17_out, S1);
  and and_13 (and_13_out, S2, not_18_out);
  not not_18 (not_18_out, S0);
  not not_19 (not_19_out, S2);
  and and_14 (and_14_out, not_19_out, S1);
  and and_15 (and_15_out, S2, not_20_out);
  not not_20 (not_20_out, S1);
  and and_16 (and_16_out, S2, not_21_out);
  not not_21 (not_21_out, S0);
  or or_2 (X6, and_1_out, and_2_out);
  or or_3 (X5, and_3_out, and_4_out, and_5_out, and_6_out);
  or or_4 (X3, not_10_out, and_7_out, and_8_out);
  or or_5 (X2, and_9_out, S1, and_10_out);
  or or_6 (X1, and_11_out, and_12_out, and_13_out);
  or or_7 (X0, and_14_out, and_15_out, and_16_out, S3);
endmodule
