// Logisim project Rand_Rom_and_7_Seg_Output.circ as structural Verilog: 1 circuit, main circuit main
module main (
  input  _0_SIGNAL,
  input  [7:0] \_0_8_BİT ,
  input  CLK,
  input  A_STATE_2_INP_SIGNAL,
  input  R_RESET,
  output [6:0] C7,
  output [6:0] C6,
  output [6:0] C5,
  output [6:0] C4,
  output [6:0] C3,
  output [6:0] C2,
  output [6:0] C1,
  output [6:0] C0,
  output X6,
  output X5,
  output X4,
  output X3,
  output X2,
  output X1,
  output X0,
  output B_STATE_2_OUTPUT
);

  wire comparator_1_eq, comparator_2_eq, multiplexer_1_out, multiplexer_3_out, not_1_out, not_2_out,
       not_3_out, not_4_out, register_1_q, register_3_q;
  wire [3:0] counter_1_q;
  wire [6:0] random_1_out;
  wire [7:0] multiplexer_2_out;
  wire [31:0] rom_1_data, rom_2_data;

  Register #(.width(1)) register_1 (
    .D(A_STATE_2_INP_SIGNAL), .en(multiplexer_1_out), .Q(register_1_q), .clk(CLK));  // open: clr
  Multiplexer multiplexer_1 (
    .in0(R_RESET), .in1(A_STATE_2_INP_SIGNAL), .out(multiplexer_1_out), .sel(A_STATE_2_INP_SIGNAL));  // open: en
  not not_1 (not_1_out, register_1_q);
  Random #(.width(7)) random_1 (.clk(CLK), .next(not_1_out), .out(random_1_out));  // open: clr
  ROM #(.addrWidth(7), .dataWidth(32)) rom_1 (.addr(random_1_out), .data(rom_1_data));  // open: sel
  ROM #(.addrWidth(7), .dataWidth(32)) rom_2 (.addr(random_1_out), .data(rom_2_data));  // open: sel
  Counter #(.width(4), .max('hf)) counter_1 (
    .Q(counter_1_q), .clk(CLK), .clr(not_2_out));  // open: load, D, count, carry
  not not_2 (not_2_out, A_STATE_2_INP_SIGNAL);
  Comparator #(.width(4), .mode("unsigned")) comparator_1 (
    .a(counter_1_q), .b(4'b1111), .eq(comparator_1_eq));  // open: gt, lt
  Multiplexer #(.select(4), .width(8)) multiplexer_2 (
    .in0(rom_2_data[7:0]), .in1(\_0_8_BİT ), .in2(rom_2_data[15:8]), .in3(\_0_8_BİT ),
    .in4(rom_2_data[23:16]), .in5(\_0_8_BİT ), .in6(rom_2_data[31:24]), .in7(\_0_8_BİT ),
    .in8(rom_1_data[7:0]), .in9(\_0_8_BİT ), .in10(rom_1_data[15:8]), .in11(\_0_8_BİT ),
    .in12(rom_1_data[23:16]), .in13(\_0_8_BİT ), .in14(rom_1_data[31:24]), .in15(\_0_8_BİT ),
    .out(multiplexer_2_out), .sel(counter_1_q));  // open: en
  Register #(.width(1)) register_2 (.D(comparator_1_eq), .Q(B_STATE_2_OUTPUT), .clk(CLK));  // open: en, clr
  Bit_Extender #(.out_width(7)) bit_extender_1 (.in(rom_2_data[31:24]), .out(C7));
  Bit_Extender #(.out_width(7)) bit_extender_2 (.in(rom_2_data[23:16]), .out(C6));
  Bit_Extender #(.out_width(7)) bit_extender_3 (.in(rom_2_data[15:8]), .out(C5));
  Bit_Extender #(.out_width(7)) bit_extender_4 (.in(rom_2_data[7:0]), .out(C4));
  Bit_Extender #(.out_width(7)) bit_extender_5 (.in(rom_1_data[31:24]), .out(C3));
  Bit_Extender #(.out_width(7)) bit_extender_6 (.in(rom_1_data[23:16]), .out(C2));
  Bit_Extender #(.out_width(7)) bit_extender_7 (.in(rom_1_data[15:8]), .out(C1));
  Bit_Extender #(.out_width(7)) bit_extender_8 (.in(rom_1_data[7:0]), .out(C0));
  Comparator comparator_2 (.a(multiplexer_2_out), .b(\_0_8_BİT ), .eq(comparator_2_eq));  // open: gt, lt
  Register #(.width(1)) register_3 (
    .D(not_3_out), .en(A_STATE_2_INP_SIGNAL), .Q(register_3_q), .clk(CLK), .clr(R_RESET));
  not not_3 (not_3_out, comparator_2_eq);
  not not_4 (not_4_out, A_STATE_2_INP_SIGNAL);
  HEX_DISPLAY hex_display_1 (
    .CLK(CLK), .X(multiplexer_3_out), .R(R_RESET), .X6(X6), .X5(X5), .X4(X4), .X3(X3), .X2(X2), .X1(X1),
    .X0(X0));
  Multiplexer multiplexer_3 (
    .in0(register_3_q), .in1(_0_SIGNAL), .out(multiplexer_3_out), .sel(not_4_out));  // open: en
  _7_Segment_Display u_7_segment_display_1 (.g(X0), .f(X1), .a(X2), .b(X3), .e(X6), .d(X5), .c(X4));  // open: dp

  // Notes on the sheet:
  //   contents of rom_1 (hex, n*v repeats v):
  //   4e000000 0 41544500 53494d00 43450000 42414241 0 0 4e000000 0 41544500 53494d00 43450000 42414241 0
  //   0 4e000000 0 41544500 53494d00 43450000 42414241 0 0 4e000000 0 41544500 53494d00 43450000 42414241
  //   0 0 4e000000 0 41544500 53494d00 43450000 42414241 0 0 4e000000 0 41544500 53494d00 43450000
  //   42414241 0 0 4e000000 0 41544500 53494d00 43450000 42414241 0 0 4e000000 0 41544500 53494d00
  //   43450000 42414241 0 0 4e000000 0 41544500 53494d00 43450000 42414241 0 0 4e000000 0 41544500
  //   53494d00 43450000 42414241 0 0 4e000000 0 41544500 53494d00 43450000 42414241 0 0 4e000000 0
  //   41544500 53494d00 43450000 42414241 0 0 4e000000 0 41544500 53494d00 43450000 42414241 0 0 4e000000
  //   0 41544500 53494d00 43450000 42414241 0 0 4e000000 0 41544500 53494d00 43450000 42414241 0 0
  //   4e000000 0 41544500 53494d00 43450000 42414241
  //   contents of rom_2 (hex, n*v repeats v):
  //   4f534d41 42414259 4f504552 4c4f4749 4f464649 5455524b 4d414e58 58585858 4f534d41 42414259 4f504552
  //   4c4f4749 4f464649 5455524b 4d414e58 58585858 4f534d41 42414259 4f504552 4c4f4749 4f464649 5455524b
  //   4d414e58 58585858 4f534d41 42414259 4f504552 4c4f4749 4f464649 5455524b 4d414e58 58585858 4f534d41
  //   42414259 4f504552 4c4f4749 4f464649 5455524b 4d414e58 58585858 4f534d41 42414259 4f504552 4c4f4749
  //   4f464649 5455524b 4d414e58 58585858 4f534d41 42414259 4f504552 4c4f4749 4f464649 5455524b 4d414e58
  //   58585858 4f534d41 42414259 4f504552 4c4f4749 4f464649 5455524b 4d414e58 58585858 4f534d41 42414259
  //   4f504552 4c4f4749 4f464649 5455524b 4d414e58 58585858 4f534d41 42414259 4f504552 4c4f4749 4f464649
  //   5455524b 4d414e58 58585858 4f534d41 42414259 4f504552 4c4f4749 4f464649 5455524b 4d414e58 58585858
  //   4f534d41 42414259 4f504552 4c4f4749 4f464649 5455524b 4d414e58 58585858 4f534d41 42414259 4f504552
  //   4c4f4749 4f464649 5455524b 4d414e58 58585858 4f534d41 42414259 4f504552 4c4f4749 4f464649 5455524b
  //   4d414e58 58585858 4f534d41 42414259 4f504552 4c4f4749 4f464649 5455524b 4d414e58 58585858 4f534d41
  //   42414259 4f504552 4c4f4749 4f464649 5455524b 4d414e58 58585858
endmodule
