// Logisim project Osman_talha_aydÄ±n_161044058.circ as structural Verilog: 1 circuit, main circuit main
module main (
);

  wire _000_out, _001_out, _010_out, _011_out, _100_out, _101_out, _110_out, and_1_out, and_2_out, and_3_out,
       and_4_out, and_5_out, and_6_out, and_7_out, and_8_out, and_9_out, and_10_out, and_11_out, and_12_out,
       and_13_out, and_14_out, and_15_out, and_16_out, and_17_out, and_18_out, and_19_out, and_20_out,
       and_21_out, and_22_out, and_23_out, and_24_out, and_25_out, and_26_out, clock_1_out, not_1_out,
       not_2_out, not_3_out, not_4_out, not_5_out, not_6_out, not_7_out, not_8_out, not_9_out, not_10_out,
       not_11_out, not_12_out, not_13_out, not_14_out, not_15_out, not_16_out, not_17_out, not_18_out,
       not_19_out, not_20_out, not_21_out, not_22_out, not_23_out, not_24_out, not_25_out, not_26_out,
       not_27_out, P1_out, P2_out, RES_out;
  wire [1:0] N0_out, STATE_q;
  wire [2:0] N0_2_out, State_2_q;

  Button P2 (.out(P2_out));
  Button P1 (.out(P1_out));
  Button RES (.out(RES_out));
  Clock #(.highDuration(5)) clock_1 (.out(clock_1_out));
  and and_1 (and_1_out, ~P2_out, ~P1_out, STATE_q[0], ~STATE_q[1]);  // AND_Gate
  and and_2 (and_2_out, ~P2_out, ~P1_out, ~STATE_q[0], STATE_q[1]);  // AND_Gate
  and and_3 (and_3_out, P1_out, STATE_q[0], ~STATE_q[1]);  // AND_Gate
  and and_4 (and_4_out, P2_out, ~P1_out, ~STATE_q[1]);  // AND_Gate
  and and_5 (and_5_out, P2_out, ~STATE_q[0], STATE_q[1]);  // AND_Gate
  and and_6 (and_6_out, ~P2_out, P1_out, ~STATE_q[0]);  // AND_Gate
  Register #(.width(2)) STATE (.D(N0_out), .en(1'b1), .Q(STATE_q), .clk(clock_1_out));  // open: clr
  or N0 (N0_out[0], and_3_out, and_4_out);
  or N1 (N0_out[1], and_5_out, and_6_out);
  Register #(.width(3)) State_2 (.D(N0_2_out), .en(1'b1), .Q(State_2_q), .clk(clock_1_out));  // open: clr
  not not_1 (not_1_out, State_2_q[1]);
  not not_2 (not_2_out, State_2_q[0]);
  not not_3 (not_3_out, and_1_out);
  not not_4 (not_4_out, State_2_q[1]);
  not not_5 (not_5_out, and_1_out);
  not not_6 (not_6_out, and_1_out);
  not not_7 (not_7_out, RES_out);
  not not_8 (not_8_out, State_2_q[2]);
  not not_9 (not_9_out, and_2_out);
  not not_10 (not_10_out, State_2_q[2]);
  not not_11 (not_11_out, State_2_q[0]);
  not not_12 (not_12_out, and_2_out);
  not not_13 (not_13_out, and_2_out);
  not not_14 (not_14_out, RES_out);
  not not_15 (not_15_out, and_1_out);
  not not_16 (not_16_out, State_2_q[2]);
  not not_17 (not_17_out, State_2_q[0]);
  not not_18 (not_18_out, and_2_out);
  not not_19 (not_19_out, State_2_q[1]);
  not not_20 (not_20_out, and_2_out);
  not not_21 (not_21_out, and_1_out);
  not not_22 (not_22_out, State_2_q[2]);
  not not_23 (not_23_out, and_1_out);
  not not_24 (not_24_out, RES_out);
  not not_25 (not_25_out, State_2_q[1]);
  not not_26 (not_26_out, State_2_q[0]);
  not not_27 (not_27_out, and_1_out);
  and and_7 (and_7_out, not_1_out, not_2_out, and_2_out, not_3_out);
  and and_8 (and_8_out, State_2_q[2], not_4_out, not_5_out);
  and and_9 (and_9_out, State_2_q[2], not_6_out, not_7_out);
  and and_10 (and_10_out, State_2_q[2], and_2_out);
  and and_11 (and_11_out, State_2_q[2], State_2_q[0]);
  and and_12 (and_12_out, State_2_q[2], State_2_q[1], and_1_out);
  and and_13 (and_13_out, not_8_out, State_2_q[0], not_9_out, and_1_out);
  and and_14 (and_14_out, not_10_out, State_2_q[1], not_11_out, not_12_out);
  and and_15 (and_15_out, State_2_q[1], not_13_out, not_14_out);
  and and_16 (and_16_out, State_2_q[1], and_1_out);
  and and_17 (and_17_out, State_2_q[1], State_2_q[0], and_2_out);
  and and_18 (and_18_out, State_2_q[2], State_2_q[0], and_2_out, not_15_out);
  and and_19 (and_19_out, State_2_q[2], State_2_q[1], and_2_out);
  and and_20 (and_20_out, not_16_out, not_17_out, not_18_out, and_1_out);
  and and_21 (and_21_out, not_19_out, State_2_q[0], not_20_out, not_21_out);
  and and_22 (and_22_out, State_2_q[0], and_2_out, and_1_out);
  and and_23 (and_23_out, not_22_out, State_2_q[1], and_2_out, not_23_out);
  and and_24 (and_24_out, State_2_q[1], State_2_q[0], not_24_out);
  and and_25 (and_25_out, State_2_q[1], State_2_q[0], and_1_out);
  and and_26 (and_26_out, State_2_q[2], not_25_out, not_26_out, and_2_out, not_27_out);
  or N2 (N0_2_out[2], and_7_out, and_8_out, and_9_out, and_10_out, and_11_out, and_12_out);
  or N1_2 (N0_2_out[1], and_13_out, and_14_out, and_15_out, and_16_out, and_17_out, and_18_out, and_19_out);
  or N0_2 (N0_2_out[0], and_20_out, and_21_out, and_22_out, and_23_out, and_24_out, and_25_out, and_26_out);
  LED led_1 (.in(_011_out));
  and _011 (_011_out, ~N0_2_out[2], N0_2_out[1], N0_2_out[0]);  // AND_Gate
  LED led_2 (.in(_010_out));
  and _010 (_010_out, ~N0_2_out[2], N0_2_out[1], ~N0_2_out[0]);  // AND_Gate
  and _001 (_001_out, ~N0_2_out[2], ~N0_2_out[1], N0_2_out[0]);  // AND_Gate
  LED led_3 (.in(_001_out));
  and _000 (_000_out, ~N0_2_out[2], ~N0_2_out[1], ~N0_2_out[0]);  // AND_Gate
  LED led_4 (.in(_000_out));
  and _100 (_100_out, N0_2_out[2], ~N0_2_out[1], ~N0_2_out[0]);  // AND_Gate
  LED led_5 (.in(_100_out));
  LED led_6 (.in(_101_out));
  and _101 (_101_out, N0_2_out[2], ~N0_2_out[1], N0_2_out[0]);  // AND_Gate
  LED led_7 (.in(_110_out));
  and _110 (_110_out, N0_2_out[2], N0_2_out[1], ~N0_2_out[0]);  // AND_Gate

  // Notes on the sheet:
  //   Pb
  //   Pa
endmodule
