// Logisim project CONTROL_UNIT.circ as structural Verilog: 1 circuit, main circuit main
module main (
  input  START,
  input  RESET,
  input  ACMP,
  input  CLK,
  output SAM,
  output LAM,
  output SFL
);

  wire and_1_out, and_2_out, and_3_out, and_4_out, and_5_out, and_6_out, and_7_out, and_8_out, and_9_out,
       and_10_out, and_11_out;
  wire [1:0] or_1_out, register_1_q;

  Register #(.width(2)) register_1 (.D(or_1_out), .en(1'b1), .Q(register_1_q), .clk(CLK));  // open: clr
  and and_1 (and_1_out, ~register_1_q[1], ~register_1_q[0], START, ACMP);  // AND_Gate
  and and_2 (and_2_out, register_1_q[1], ~register_1_q[0]);  // AND_Gate
  and and_3 (and_3_out, register_1_q[1], register_1_q[0], ~RESET);  // AND_Gate
  and and_4 (and_4_out, ~register_1_q[1], register_1_q[0], ACMP);  // AND_Gate
  and and_5 (and_5_out, register_1_q[1], ~register_1_q[0], ~ACMP);  // AND_Gate
  and and_6 (and_6_out, register_1_q[1], register_1_q[0], ~RESET);  // AND_Gate
  or or_1 (or_1_out[0], and_1_out, and_2_out, and_3_out);
  or or_2 (or_1_out[1], and_4_out, and_5_out, and_6_out);
  and and_7 (and_7_out, or_1_out[0], ~or_1_out[1]);  // AND_Gate
  and and_8 (and_8_out, ~or_1_out[0], or_1_out[1]);  // AND_Gate
  and and_9 (and_9_out, ~or_1_out[0], ~or_1_out[1]);  // AND_Gate
  and and_10 (and_10_out, or_1_out[0], ~or_1_out[1]);  // AND_Gate
  and and_11 (and_11_out, ~or_1_out[0], or_1_out[1]);  // AND_Gate
  and and_12 (SFL, or_1_out[0], ~or_1_out[1]);  // AND_Gate
  or or_3 (SAM, and_7_out, and_8_out);
  or or_4 (LAM, and_9_out, and_10_out, and_11_out);
endmodule
