// Logisim project DATAPATH.circ as structural Verilog: 1 circuit, main circuit main
module main (
  input  SAM,
  input  [15:0] _0,
  input  [15:0] FA_Inp,
  input  [15:0] FM_Inp,
  input  [15:0] minus_1_Inp,
  input  [15:0] B_Inp,
  input  LAM,
  input  SFL,
  input  CLK,
  output ACMP,
  output [15:0] FM_OUT
);

  wire and_1_out, and_2_out, and_3_out, and_4_out, and_5_out, and_6_out, comparator_1_lt, comparator_2_lt,
       comparator_3_eq, or_1_out;
  wire [15:0] adder_1_out, multiplexer_1_out, multiplexer_2_out, multiplexer_3_out, multiplexer_4_out,
       multiplexer_5_out, multiplexer_6_out, multiplexer_7_out, negator_1_out, negator_2_out, register_1_q,
       register_2_q, register_3_q;

  Comparator #(.width(16)) comparator_1 (.a(FA_Inp), .b(_0), .lt(comparator_1_lt));  // open: gt, eq
  Comparator #(.width(16)) comparator_2 (.a(B_Inp), .b(_0), .lt(comparator_2_lt));  // open: gt, eq
  Negator #(.width(16)) negator_1 (.in(FA_Inp), .out(negator_1_out));
  Multiplexer #(.width(16)) multiplexer_1 (
    .in0(FA_Inp), .in1(negator_1_out), .out(multiplexer_1_out), .sel(comparator_1_lt));  // open: en
  Multiplexer #(.width(16)) multiplexer_2 (
    .in0(adder_1_out), .in1(register_1_q), .out(multiplexer_2_out), .sel(SFL));  // open: en
  Multiplexer #(.width(16)) multiplexer_3 (
    .in0(multiplexer_1_out), .in1(multiplexer_2_out), .out(multiplexer_3_out), .sel(SAM));  // open: en
  Multiplexer #(.width(16)) multiplexer_4 (
    .in0(register_2_q), .in1(adder_1_out), .out(multiplexer_4_out), .sel(SFL));  // open: en
  Multiplexer #(.width(16)) multiplexer_5 (
    .in0(FM_Inp), .in1(multiplexer_4_out), .out(multiplexer_5_out), .sel(SAM));  // open: en
  Register #(.width(16)) register_1 (.D(multiplexer_3_out), .en(LAM), .Q(register_1_q), .clk(CLK));  // open: clr
  Register #(.width(16)) register_2 (.D(multiplexer_5_out), .en(LAM), .Q(register_2_q), .clk(CLK));  // open: clr
  Register #(.width(16)) register_3 (.D(register_2_q), .en(LAM), .Q(register_3_q), .clk(CLK));  // open: clr
  Multiplexer #(.width(16)) multiplexer_6 (
    .in0(register_1_q), .in1(register_2_q), .out(multiplexer_6_out), .sel(SFL));  // open: en
  Multiplexer #(.width(16)) multiplexer_7 (
    .in0(minus_1_Inp), .in1(B_Inp), .out(multiplexer_7_out), .sel(SFL));  // open: en
  and and_1 (and_1_out, ~comparator_2_lt, ~1'b0);  // AND_Gate
  and and_2 (and_2_out, comparator_1_lt, 1'b1);
  and and_3 (and_3_out, comparator_2_lt, 1'b1);
  and and_4 (and_4_out, comparator_1_lt, 1'b1);
  Adder #(.width(16)) adder_1 (.a(multiplexer_6_out), .b(multiplexer_7_out), .out(adder_1_out));  // open: cin, cout
  and and_5 (and_5_out, and_1_out, and_2_out);
  and and_6 (and_6_out, and_3_out, and_4_out);
  Comparator #(.width(16)) comparator_3 (.a(register_1_q), .b(_0), .eq(comparator_3_eq));  // open: gt, lt
  Negator #(.width(16)) negator_2 (.in(register_3_q), .out(negator_2_out));
  Multiplexer #(.width(16)) multiplexer_8 (
    .in0(register_3_q), .in1(negator_2_out), .out(FM_OUT), .sel(or_1_out));  // open: en
  or or_1 (or_1_out, and_5_out, and_6_out);
  not not_1 (ACMP, comparator_3_eq);
endmodule
