// Logisim project Multiplier.circ as structural Verilog: 1 circuit, main circuit main
module main (
  input  [15:0] _0,
  input  [15:0] FA_Inp,
  input  [15:0] FM_Inp,
  input  [15:0] minus_1_Inp,
  input  [15:0] B_Inp,
  output [15:0] LM_OUT
);

  wire clock_1_out, main_1_lam, main_1_sam, main_1_sfl, main_2_acmp, RESET_out, START_out;

  Button START (.out(START_out));
  Button RESET (.out(RESET_out));
  Clock clock_1 (.out(clock_1_out));
  CONTROL_UNIT_main main_1 (
    .START(START_out), .RESET(RESET_out), .ACMP(main_2_acmp), .CLK(clock_1_out), .SAM(main_1_sam),
    .LAM(main_1_lam), .SFL(main_1_sfl));
  DATAPATH_main main_2 (
    .SAM(main_1_sam), ._0(_0), .FA_Inp(FA_Inp), .FM_Inp(FM_Inp), .minus_1_Inp(minus_1_Inp), .B_Inp(B_Inp),
    .LAM(main_1_lam), .SFL(main_1_sfl), .CLK(clock_1_out), .ACMP(main_2_acmp), .FM_OUT(LM_OUT));
endmodule
